// Logisim project cache.circ as structural Verilog: 1 circuit
module DirectMappedCache (
);

  wire Address_2_p1, comparator_1_p2, constant_1_p1, Data_In_p1, Data_Out_2_p1, FIFO_Counter_p1, ram_2_p1,
       ram_3_p1, splitter_1_p2, splitter_1_p3, splitter_1_p5, splitter_2_p1, splitter_2_p3;

  // Register Address: pin names not known
  // Tunnel Address_2: pin names not known; wires that end beside it: Address_2_p1
  // Splitter splitter_1: pin names not known; wires that end beside it: Address_2_p1, splitter_1_p2, splitter_1_p3, splitter_1_p2, splitter_1_p5
  // Splitter splitter_2: pin names not known; wires that end beside it: splitter_2_p1, splitter_2_p1, splitter_2_p3
  // Constant constant_1: pin names not known; wires that end beside it: constant_1_p1
  // RAM ram_1: pin names not known; wires that end beside it: splitter_1_p5
  // RAM ram_2: pin names not known; wires that end beside it: ram_2_p1, splitter_2_p3
  // Register FIFO_Counter: pin names not known; wires that end beside it: FIFO_Counter_p1
  // Adder adder_1: pin names not known
  // Multiplexer multiplexer_1: pin names not known
  // Comparator comparator_1: pin names not known; wires that end beside it: ram_2_p1, comparator_1_p2
  // Multiplexer multiplexer_2: pin names not known; wires that end beside it: constant_1_p1
  // Tunnel Hit: pin names not known; wires that end beside it: comparator_1_p2
  // Tunnel Write_Enable: pin names not known; wires that end beside it: FIFO_Counter_p1
  // Register Data_Out: pin names not known; wires that end beside it: splitter_1_p3
  // Tunnel Data_Out_2: pin names not known; wires that end beside it: Data_Out_2_p1, Data_Out_2_p1
  // RAM ram_3: pin names not known; wires that end beside it: ram_3_p1, ram_3_p1
  // Tunnel Data_In: pin names not known; wires that end beside it: Data_In_p1, Data_In_p1
endmodule
