// Logisim project cpu_risc_v.circ as structural Verilog
module main (
  input  ResetPC,
  input  ENABLE_WRITE
);

  wire clock_1_out, cu_1_jump, decoder_unit_1_aluimm, decoder_unit_1_storem, ex_mem_pipeline_1_o_jump,
       ex_mem_pipeline_1_o_storem, id_ex_pipeline_1_o_storem, Write_F, Write_R, Write_V;
  wire [1:0] decoder_unit_1_loadr, decoder_unit_1_unit, ex_mem_pipeline_1_o_unit,
       ex_mem_pipeline_1_o_write_unit, id_ex_pipeline_1_o_unit, id_ex_pipeline_1_o_writeunit,
       mem_wb_pipeline_1_o_unit, mem_wb_pipeline_1_o_write_unit;
  wire [4:0] decoder_unit_1_rd, decoder_unit_1_rs1, decoder_unit_1_rs2, ex_mem_pipeline_1_o_rd,
       id_ex_pipeline_1_o_frs2, id_ex_pipeline_1_o_rd, mem_wb_pipeline_1_o_rd;
  wire [6:0] decoder_unit_1_funct37, decoder_unit_1_opcode, id_ex_pipeline_1_o_funct73,
       id_ex_pipeline_1_o_opcode;
  wire [23:0] id_ex_pipeline_1_o_pc, if_id_pipeline_1_o_pc, MemW, multiplexer_1_out, PC_q;
  wire [31:0] alu_1_result, cu_1_result, Data_F, Data_I, decoder_unit_1_imm, ex_mem_pipeline_1_o_alu,
       ex_mem_pipeline_1_o_cu, ex_mem_pipeline_1_o_fpalu, ex_mem_pipeline_1_o_valu_1,
       ex_mem_pipeline_1_o_valu_2, ex_mem_pipeline_1_o_valu_3, Float_outputx, Float_outputy,
       forwarding_unit_1_op1, forwarding_unit_1_op2, forwarding_unit_2_op1, forwarding_unit_2_op2,
       fpalu_1_result, id_ex_pipeline_1_o_fop1, id_ex_pipeline_1_o_fop2, id_ex_pipeline_1_o_imm,
       id_ex_pipeline_1_o_iop1, id_ex_pipeline_1_o_iop2, id_ex_pipeline_1_o_xop1, id_ex_pipeline_1_o_xop2,
       id_ex_pipeline_1_o_xop3, id_ex_pipeline_1_o_yop1, id_ex_pipeline_1_o_yop2, id_ex_pipeline_1_o_yop3,
       if_id_pipeline_1_o_instruction, Interger_outputx, Interger_outputy, mem_wb_pipeline_1_o_alu,
       mem_wb_pipeline_1_o_cu, mem_wb_pipeline_1_o_mu, mem_wb_pipeline_1_o_valu_1,
       mem_wb_pipeline_1_o_valu_2, mem_wb_pipeline_1_o_valu_3, MemData, mu_1_result, ram_1_dout, valu_1_out1,
       valu_1_out2, valu_1_out3, vector_register_file_1_outputx1, vector_register_file_1_outputx2,
       vector_register_file_1_outputx3, vector_register_file_1_outputy1, vector_register_file_1_outputy2,
       vector_register_file_1_outputy3;
  wire [31:24] ex_mem_pipeline_1_o_mu;

  Clock clock_1 (.out(clock_1_out));
  Counter #(.max('hffffff), .width(24)) PC (
    .load(ex_mem_pipeline_1_o_jump), .D(ex_mem_pipeline_1_o_cu[23:0]), .Q(PC_q), .clk(clock_1_out),
    .clr(ResetPC));  // open: count, carry, up
  Multiplexer #(.width(24)) multiplexer_1 (
    .in0(PC_q), .in1(MemW), .out(multiplexer_1_out), .sel(ex_mem_pipeline_1_o_storem));
  RAM #(.addrWidth(24), .dataWidth(32), .enables("line")) ram_1 (
    .addr(multiplexer_1_out), .we(ex_mem_pipeline_1_o_storem), .clk(clock_1_out), .din(MemData),
    .dout(ram_1_dout));
  IF_ID_Pipeline if_id_pipeline_1 (
    .ENABLE_WRITE(ENABLE_WRITE), .INSTRUCTION(ram_1_dout), .PC(PC_q), .CLOCK(clock_1_out),
    .O_PC(if_id_pipeline_1_o_pc), .O_INSTRUCTION(if_id_pipeline_1_o_instruction));
  decoder_unit decoder_unit_1 (
    .Instruction(if_id_pipeline_1_o_instruction), .Unit(decoder_unit_1_unit), .Opcode(decoder_unit_1_opcode),
    .RD(decoder_unit_1_rd), .RS1(decoder_unit_1_rs1), .RS2(decoder_unit_1_rs2),
    .Funct37(decoder_unit_1_funct37), .LoadR(decoder_unit_1_loadr), .ALUImm(decoder_unit_1_aluimm),
    .StoreM(decoder_unit_1_storem), .Imm(decoder_unit_1_imm));
  vector_register_file vector_register_file_1 (
    .RD(mem_wb_pipeline_1_o_rd), .Write(Write_V), .RX(decoder_unit_1_rs1), .RY(decoder_unit_1_rs2),
    .Data1(mem_wb_pipeline_1_o_valu_1), .Data2(mem_wb_pipeline_1_o_valu_2),
    .Data3(mem_wb_pipeline_1_o_valu_3), .Clock(clock_1_out), .OutputY1(vector_register_file_1_outputy1),
    .OutputY2(vector_register_file_1_outputy2), .OutputY3(vector_register_file_1_outputy3),
    .OutputX1(vector_register_file_1_outputx1), .OutputX2(vector_register_file_1_outputx2),
    .OutputX3(vector_register_file_1_outputx3));
  register_file Float (
    .Data(Data_F), .RD(mem_wb_pipeline_1_o_rd), .Write(Write_F), .RX(decoder_unit_1_rs1),
    .RY(decoder_unit_1_rs2), .Clock(clock_1_out), .OutputX(Float_outputx), .OutputY(Float_outputy));
  register_file Interger (
    .Data(Data_I), .RD(mem_wb_pipeline_1_o_rd), .Write(Write_R), .RX(decoder_unit_1_rs1),
    .RY(decoder_unit_1_rs2), .Clock(clock_1_out), .OutputX(Interger_outputx), .OutputY(Interger_outputy));
  forwarding_unit forwarding_unit_1 (
    .is_immediate(decoder_unit_1_aluimm), .rs1_value(Float_outputx), .rs2_value(Float_outputy),
    .imm_value(decoder_unit_1_imm), .rd(id_ex_pipeline_1_o_rd), .rs1(decoder_unit_1_rs1),
    .rs2(decoder_unit_1_rs2), .forwarded_value(fpalu_1_result), .op1(forwarding_unit_1_op1),
    .op2(forwarding_unit_1_op2));
  forwarding_unit forwarding_unit_2 (
    .is_immediate(decoder_unit_1_aluimm), .rs1_value(Interger_outputx), .rs2_value(Interger_outputy),
    .imm_value(decoder_unit_1_imm), .rd(id_ex_pipeline_1_o_rd), .rs1(decoder_unit_1_rs1),
    .rs2(decoder_unit_1_rs2), .forwarded_value(alu_1_result), .op1(forwarding_unit_2_op1),
    .op2(forwarding_unit_2_op2));
  ID_EX_Pipeline id_ex_pipeline_1 (
    .ENABLE_WRITE(ENABLE_WRITE), .RD(decoder_unit_1_rd), .IOP2(forwarding_unit_2_op2),
    .IMM(decoder_unit_1_imm), .OPCODE(decoder_unit_1_opcode), .WriteUnit(decoder_unit_1_loadr),
    .PC(if_id_pipeline_1_o_pc), .STOREM(decoder_unit_1_storem), .UNIT(decoder_unit_1_unit),
    .XOP1(vector_register_file_1_outputx3), .XOP2(vector_register_file_1_outputx1),
    .XOP3(vector_register_file_1_outputx2), .YOP1(vector_register_file_1_outputy1),
    .YOP2(vector_register_file_1_outputy2), .YOP3(vector_register_file_1_outputy3),
    .FOP1(forwarding_unit_1_op1), .FOP2(forwarding_unit_1_op2), .FRS2(decoder_unit_1_rs2),
    .IOP1(forwarding_unit_2_op1), .FUNCT73(decoder_unit_1_funct37), .CLOCK(clock_1_out),
    .O_FUNCT73(id_ex_pipeline_1_o_funct73), .O_IOP2(id_ex_pipeline_1_o_iop2), .O_IMM(id_ex_pipeline_1_o_imm),
    .O_OPCODE(id_ex_pipeline_1_o_opcode), .O_WriteUnit(id_ex_pipeline_1_o_writeunit),
    .O_PC(id_ex_pipeline_1_o_pc), .O_RD(id_ex_pipeline_1_o_rd), .O_XOP1(id_ex_pipeline_1_o_xop1),
    .O_XOP2(id_ex_pipeline_1_o_xop2), .O_XOP3(id_ex_pipeline_1_o_xop3), .O_YOP1(id_ex_pipeline_1_o_yop1),
    .O_YOP2(id_ex_pipeline_1_o_yop2), .O_YOP3(id_ex_pipeline_1_o_yop3), .O_FOP1(id_ex_pipeline_1_o_fop1),
    .O_FOP2(id_ex_pipeline_1_o_fop2), .O_FRS2(id_ex_pipeline_1_o_frs2), .O_IOP1(id_ex_pipeline_1_o_iop1),
    .O_STOREM(id_ex_pipeline_1_o_storem), .O_UNIT(id_ex_pipeline_1_o_unit));
  VALU valu_1 (
    .Op1_1(id_ex_pipeline_1_o_xop2), .Op1_2(id_ex_pipeline_1_o_xop3), .Op1_3(id_ex_pipeline_1_o_xop1),
    .Op2_1(id_ex_pipeline_1_o_yop1), .Op2_2(id_ex_pipeline_1_o_yop2), .Op2_3(id_ex_pipeline_1_o_yop3),
    .Func37(id_ex_pipeline_1_o_funct73), .Out1(valu_1_out1), .Out2(valu_1_out2), .Out3(valu_1_out3));
  FPALU fpalu_1 (
    .rs2(id_ex_pipeline_1_o_frs2), .Funct73(id_ex_pipeline_1_o_funct73), .Op1(id_ex_pipeline_1_o_fop1),
    .Op2(id_ex_pipeline_1_o_fop2), .result(fpalu_1_result));
  ALU alu_1 (
    .Op1(id_ex_pipeline_1_o_iop1), .Op2(id_ex_pipeline_1_o_iop2), .Func37(id_ex_pipeline_1_o_funct73),
    .Result(alu_1_result));  // open: CSR
  MU mu_1 (
    .IMM(id_ex_pipeline_1_o_imm), .Funct73(id_ex_pipeline_1_o_funct73), .RS1(id_ex_pipeline_1_o_iop1),
    .Result(mu_1_result));
  CU cu_1 (
    .PC(id_ex_pipeline_1_o_pc), .RS1(id_ex_pipeline_1_o_iop1), .RS2(id_ex_pipeline_1_o_iop2),
    .Opcode(id_ex_pipeline_1_o_opcode), .IMM(id_ex_pipeline_1_o_imm), .Funct73(id_ex_pipeline_1_o_funct73),
    .Jump(cu_1_jump), .Result(cu_1_result));
  EX_MEM_Pipeline ex_mem_pipeline_1 (
    .enable_write(ENABLE_WRITE), .clock(clock_1_out), .valu_1(valu_1_out1), .valu_2(valu_1_out2),
    .value_3(valu_1_out3), .rd(id_ex_pipeline_1_o_rd), .pc_inst(id_ex_pipeline_1_o_pc),
    .unit(id_ex_pipeline_1_o_unit), .mem_write_info(id_ex_pipeline_1_o_iop2), .cu(cu_1_result),
    .mu(mu_1_result), .alu(alu_1_result), .fpalu(fpalu_1_result), .jump(cu_1_jump),
    .write_unit(id_ex_pipeline_1_o_writeunit), .storem(id_ex_pipeline_1_o_storem),
    .o_mem_write_info(MemData), .o_rd(ex_mem_pipeline_1_o_rd), .o_cu(ex_mem_pipeline_1_o_cu),
    .o_mu({ex_mem_pipeline_1_o_mu, MemW}), .o_jump(ex_mem_pipeline_1_o_jump),
    .o_storem(ex_mem_pipeline_1_o_storem), .o_alu(ex_mem_pipeline_1_o_alu),
    .o_fpalu(ex_mem_pipeline_1_o_fpalu), .o_valu_1(ex_mem_pipeline_1_o_valu_1),
    .o_valu_2(ex_mem_pipeline_1_o_valu_2), .o_write_unit(ex_mem_pipeline_1_o_write_unit),
    .o_valu_3(ex_mem_pipeline_1_o_valu_3), .o_unit(ex_mem_pipeline_1_o_unit));  // open: o_pc_instruction
  MEM_WB_Pipeline mem_wb_pipeline_1 (
    .clock(clock_1_out), .rd(ex_mem_pipeline_1_o_rd), .valu_output_1(ex_mem_pipeline_1_o_valu_1),
    .valu_output_2(ex_mem_pipeline_1_o_valu_2), .value_output_3(ex_mem_pipeline_1_o_valu_3),
    .cu(ex_mem_pipeline_1_o_cu), .mu({ex_mem_pipeline_1_o_mu, MemW}), .alu(ex_mem_pipeline_1_o_alu),
    .fpalu(ex_mem_pipeline_1_o_fpalu), .write_unit(ex_mem_pipeline_1_o_write_unit),
    .unit(ex_mem_pipeline_1_o_unit), .ENABLE_WRITE(ENABLE_WRITE), .o_valu_1(mem_wb_pipeline_1_o_valu_1),
    .o_valu_2(mem_wb_pipeline_1_o_valu_2), .o_valu_3(mem_wb_pipeline_1_o_valu_3), .o_fpalu(Data_F),
    .o_rd(mem_wb_pipeline_1_o_rd), .o_write_unit(mem_wb_pipeline_1_o_write_unit),
    .o_unit(mem_wb_pipeline_1_o_unit), .o_cu(mem_wb_pipeline_1_o_cu), .o_mu(mem_wb_pipeline_1_o_mu),
    .o_alu(mem_wb_pipeline_1_o_alu));  // open: store_flag, o_store_flag
  Multiplexer #(.select(2), .width(32)) multiplexer_2 (
    .in0(mem_wb_pipeline_1_o_alu), .in1(mem_wb_pipeline_1_o_mu), .in2(mem_wb_pipeline_1_o_cu), .out(Data_I),
    .sel(mem_wb_pipeline_1_o_unit));  // open: in3
  Decoder #(.enable("false"), .select(2)) decoder_1 (
    .out1(Write_R), .out2(Write_V), .out3(Write_F), .sel(mem_wb_pipeline_1_o_write_unit));  // open: out0

  // Notes on the sheet:
  //   StoreFlag
  //   JUMP/BRANCH
  //   Enable register Writting
endmodule

module IF_ID_Pipeline (
  input  [31:0] INSTRUCTION,
  input  ENABLE_WRITE,
  input  [23:0] PC,
  input  CLOCK,
  output [31:0] O_INSTRUCTION,
  output [23:0] O_PC
);

  Register #(.width(32)) register_1 (.D(INSTRUCTION), .en(ENABLE_WRITE), .Q(O_INSTRUCTION), .clk(CLOCK), .clr(1'b0));
  Register #(.width(24)) register_2 (.D(PC), .en(ENABLE_WRITE), .Q(O_PC), .clk(CLOCK), .clr(1'b0));
endmodule

module ID_EX_Pipeline (
  input  [6:0] FUNCT73,
  input  ENABLE_WRITE,
  input  STOREM,
  input  [1:0] UNIT,
  input  [31:0] XOP1,
  input  [31:0] XOP2,
  input  [31:0] XOP3,
  input  [31:0] YOP1,
  input  [31:0] YOP2,
  input  [31:0] YOP3,
  input  [31:0] FOP1,
  input  [31:0] FOP2,
  input  [4:0] FRS2,
  input  [31:0] IOP1,
  input  [31:0] IOP2,
  input  [31:0] IMM,
  input  [6:0] OPCODE,
  input  [1:0] WriteUnit,
  input  [23:0] PC,
  input  CLOCK,
  input  [4:0] RD,
  output [6:0] O_FUNCT73,
  output O_STOREM,
  output [1:0] O_UNIT,
  output [31:0] O_XOP1,
  output [31:0] O_XOP2,
  output [31:0] O_XOP3,
  output [31:0] O_YOP1,
  output [31:0] O_YOP2,
  output [31:0] O_YOP3,
  output [31:0] O_FOP1,
  output [31:0] O_FOP2,
  output [4:0] O_FRS2,
  output [31:0] O_IOP1,
  output [31:0] O_IOP2,
  output [31:0] O_IMM,
  output [6:0] O_OPCODE,
  output [1:0] O_WriteUnit,
  output [23:0] O_PC,
  output [4:0] O_RD
);

  Register #(.width(7)) register_1 (.D(FUNCT73), .en(ENABLE_WRITE), .Q(O_FUNCT73), .clk(CLOCK), .clr(1'b0));
  Register #(.width(1)) register_2 (.D(STOREM), .en(ENABLE_WRITE), .Q(O_STOREM), .clk(CLOCK), .clr(1'b0));
  Register #(.width(2)) register_3 (.D(UNIT), .en(ENABLE_WRITE), .Q(O_UNIT), .clk(CLOCK), .clr(1'b0));
  Register #(.width(32)) register_4 (.D(XOP1), .en(ENABLE_WRITE), .Q(O_XOP1), .clk(CLOCK), .clr(1'b0));
  Register #(.width(32)) register_5 (.D(XOP2), .en(ENABLE_WRITE), .Q(O_XOP2), .clk(CLOCK), .clr(1'b0));
  Register #(.width(32)) register_6 (.D(XOP3), .en(ENABLE_WRITE), .Q(O_XOP3), .clk(CLOCK), .clr(1'b0));
  Register #(.width(32)) register_7 (.D(YOP1), .en(ENABLE_WRITE), .Q(O_YOP1), .clk(CLOCK), .clr(1'b0));
  Register #(.width(32)) register_8 (.D(YOP2), .en(ENABLE_WRITE), .Q(O_YOP2), .clk(CLOCK), .clr(1'b0));
  Register #(.width(32)) register_9 (.D(YOP3), .en(ENABLE_WRITE), .Q(O_YOP3), .clk(CLOCK), .clr(1'b0));
  Register #(.width(32)) register_10 (.D(FOP1), .en(ENABLE_WRITE), .Q(O_FOP1), .clk(CLOCK), .clr(1'b0));
  Register #(.width(32)) register_11 (.D(FOP2), .en(ENABLE_WRITE), .Q(O_FOP2), .clk(CLOCK), .clr(1'b0));
  Register #(.width(5)) register_12 (.D(FRS2), .en(ENABLE_WRITE), .Q(O_FRS2), .clk(CLOCK), .clr(1'b0));
  Register #(.width(32)) register_13 (.D(IOP1), .en(ENABLE_WRITE), .Q(O_IOP1), .clk(CLOCK), .clr(1'b0));
  Register #(.width(32)) register_14 (.D(IOP2), .en(ENABLE_WRITE), .Q(O_IOP2), .clk(CLOCK), .clr(1'b0));
  Register #(.width(32)) register_15 (.D(IMM), .en(ENABLE_WRITE), .Q(O_IMM), .clk(CLOCK), .clr(1'b0));
  Register #(.width(7)) register_16 (.D(OPCODE), .en(ENABLE_WRITE), .Q(O_OPCODE), .clk(CLOCK), .clr(1'b0));
  Register #(.width(2)) register_17 (.D(WriteUnit), .en(ENABLE_WRITE), .Q(O_WriteUnit), .clk(CLOCK), .clr(1'b0));
  Register #(.width(24)) register_18 (.D(PC), .en(ENABLE_WRITE), .Q(O_PC), .clk(CLOCK), .clr(1'b0));
  Register #(.width(5)) register_19 (.D(RD), .en(ENABLE_WRITE), .Q(O_RD), .clk(CLOCK), .clr(1'b0));
endmodule

module EX_MEM_Pipeline (
  input  clock,
  input  enable_write,
  input  [31:0] cu,
  input  [1:0] unit,
  input  [31:0] mu,
  input  [31:0] alu,
  input  [31:0] fpalu,
  input  [31:0] valu_1,
  input  [31:0] valu_2,
  input  [31:0] value_3,
  input  jump,
  input  [1:0] write_unit,
  input  storem,
  input  [31:0] mem_write_info,
  input  [23:0] pc_inst,
  input  [4:0] rd,
  output [31:0] o_cu,
  output [1:0] o_unit,
  output [31:0] o_mu,
  output [31:0] o_alu,
  output [31:0] o_fpalu,
  output [31:0] o_valu_1,
  output [31:0] o_valu_2,
  output [31:0] o_valu_3,
  output o_jump,
  output [1:0] o_write_unit,
  output o_storem,
  output [31:0] o_mem_write_info,
  output [23:0] o_pc_instruction,
  output [4:0] o_rd
);

  Register #(.width(32)) cu_result (.D(cu), .en(enable_write), .Q(o_cu), .clk(clock), .clr(1'b0));
  Register #(.width(2)) register_1 (.D(unit), .en(enable_write), .Q(o_unit), .clk(clock), .clr(1'b0));
  Register #(.width(32)) mu_result (.D(mu), .en(enable_write), .Q(o_mu), .clk(clock), .clr(1'b0));
  Register #(.width(32)) alu_result (.D(alu), .en(enable_write), .Q(o_alu), .clk(clock), .clr(1'b0));
  Register #(.width(32)) fpalu_result (.D(fpalu), .en(enable_write), .Q(o_fpalu), .clk(clock), .clr(1'b0));
  Register #(.width(1)) register_2 (.D(jump), .en(enable_write), .Q(o_jump), .clk(clock), .clr(1'b0));
  Register #(.width(2)) register_3 (.D(write_unit), .en(enable_write), .Q(o_write_unit), .clk(clock), .clr(1'b0));
  Register #(.width(1)) register_4 (.D(storem), .en(enable_write), .Q(o_storem), .clk(clock), .clr(1'b0));
  Register #(.width(32)) register_5 (
    .D(mem_write_info), .en(enable_write), .Q(o_mem_write_info), .clk(clock), .clr(1'b0));
  Register #(.width(24)) register_6 (.D(pc_inst), .en(enable_write), .Q(o_pc_instruction), .clk(clock), .clr(1'b0));
  Register #(.width(5)) register_7 (.D(rd), .en(enable_write), .Q(o_rd), .clk(clock), .clr(1'b0));
  vector_register vector_register_1 (
    .Clock(clock), .WriteEnable(enable_write), .Clear(1'b0), .Input_0(valu_1), .Input_1(valu_2),
    .Input_2(value_3), .Output_0(o_valu_1), .Output_1(o_valu_2), .Output_2(o_valu_3));

  // Notes on the sheet:
  //   the pc value the instruction in the pipeline came with, if need it
endmodule

module MEM_WB_Pipeline (
  input  clock,
  input  store_flag,
  input  [1:0] unit,
  input  [31:0] cu,
  input  [31:0] mu,
  input  [31:0] alu,
  input  [31:0] fpalu,
  input  [31:0] valu_output_1,
  input  [31:0] valu_output_2,
  input  [31:0] value_output_3,
  input  [1:0] write_unit,
  input  ENABLE_WRITE,
  input  [4:0] rd,
  output o_store_flag,
  output [1:0] o_unit,
  output [31:0] o_cu,
  output [31:0] o_mu,
  output [31:0] o_alu,
  output [31:0] o_fpalu,
  output [31:0] o_valu_1,
  output [31:0] o_valu_2,
  output [31:0] o_valu_3,
  output [1:0] o_write_unit,
  output [4:0] o_rd
);

  Register #(.width(1)) register_1 (.D(store_flag), .Q(o_store_flag), .clk(clock), .clr(1'b0));  // open: en
  Register #(.width(2)) register_2 (.D(unit), .en(ENABLE_WRITE), .Q(o_unit), .clk(clock), .clr(1'b0));
  Register #(.width(32)) cu_result (.D(cu), .en(ENABLE_WRITE), .Q(o_cu), .clk(clock), .clr(1'b0));
  Register #(.width(32)) mu_result (.D(mu), .en(ENABLE_WRITE), .Q(o_mu), .clk(clock), .clr(1'b0));
  Register #(.width(32)) alu_result (.D(alu), .en(ENABLE_WRITE), .Q(o_alu), .clk(clock), .clr(1'b0));
  Register #(.width(32)) fpalu_result (.D(fpalu), .en(ENABLE_WRITE), .Q(o_fpalu), .clk(clock), .clr(1'b0));
  Register #(.width(2)) register_3 (.D(write_unit), .en(ENABLE_WRITE), .Q(o_write_unit), .clk(clock), .clr(1'b0));
  Register #(.width(5)) register_4 (.D(rd), .en(ENABLE_WRITE), .Q(o_rd), .clk(clock), .clr(1'b0));
  vector_register vector_register_1 (
    .Clock(clock), .WriteEnable(ENABLE_WRITE), .Clear(1'b0), .Input_0(valu_output_1),
    .Input_1(valu_output_2), .Input_2(value_output_3), .Output_0(o_valu_1), .Output_1(o_valu_2),
    .Output_2(o_valu_3));
endmodule

module FPALU (
  input  [6:0] Funct73,
  input  [31:0] Op1,
  input  [31:0] Op2,
  input  [4:0] rs2,
  output [31:0] result
);

  wire fpcomparator_1_p3, fpcomparator_1_p4, or_1_out;
  wire [1:0] fp_convert_detector_1_out_3, fp_mmnsc_detector_1_out_2, or_2_out;
  wire [3:0] fp_convert_reducer_1_reduced, fp_mmnsc_reducer_1_out_2;
  wire [31:0] bit_extender_1_out, bit_extender_2_out, bit_extender_3_out, fp_min_max_1_max, fp_min_max_1_min,
       fp_signed_inject_1_out_3, fp_signed_inject_negate_1_out_3, fp_signed_inject_xor_1_out_3,
       fpadder_1_out, fpdivider_1_out, fpmultiplier_1_out, fpsqr_wrapper_1_out_2, fpsubtractor_1_out,
       fptoint_1_p2, inttofp_1_p2, inttofp_2_p2, multiplexer_1_out, multiplexer_2_out, multiplexer_3_out;

  FPAdder fpadder_1 (.a(Op1), .b(Op2), .out(fpadder_1_out));
  FPSubtractor fpsubtractor_1 (.a(Op1), .b(Op2), .out(fpsubtractor_1_out));
  FPMultiplier fpmultiplier_1 (.a(Op1), .b(Op2), .out(fpmultiplier_1_out));
  FPDivider fpdivider_1 (.a(Op1), .b(Op2), .out(fpdivider_1_out));
  fpsqr_wrapper fpsqr_wrapper_1 (.operand1(Op1), .out_2(fpsqr_wrapper_1_out_2));
  // FPComparator fpcomparator_1: pin names not known; wires that end beside it: Op1, Op2, fpcomparator_1_p3, fpcomparator_1_p4
  fp_signed_inject fp_signed_inject_1 (.in_1(Op1), .in_2(Op2), .out_3(fp_signed_inject_1_out_3));
  fp_signed_inject_negate fp_signed_inject_negate_1 (.in_1(Op1), .in_2(Op2), .out_3(fp_signed_inject_negate_1_out_3));
  fp_signed_inject_xor fp_signed_inject_xor_1 (.in_1(Op1), .in_2(Op2), .out_3(fp_signed_inject_xor_1_out_3));
  // IntToFP #(.width(32)) inttofp_1: pin names not known; wires that end beside it: Op1, inttofp_1_p2
  // IntToFP #(.mode("unsigned"), .width(32)) inttofp_2: pin names not known; wires that end beside it: Op1, inttofp_2_p2
  // FPToInt #(.width(32)) fptoint_1: pin names not known; wires that end beside it: Op1, fptoint_1_p2
  fp_min_max fp_min_max_1 (.operand2(Op2), .operand1(Op1), .max(fp_min_max_1_max), .min(fp_min_max_1_min));
  assign bit_extender_1_out = {{31{1'b0}}, or_1_out};  // Bit_Extender bit_extender_1
  or or_1 (or_1_out, fpcomparator_1_p3, fpcomparator_1_p4);
  assign bit_extender_2_out = {{31{1'b0}}, fpcomparator_1_p3};  // Bit_Extender bit_extender_2
  assign bit_extender_3_out = {{31{1'b0}}, fpcomparator_1_p4};  // Bit_Extender bit_extender_3
  Multiplexer #(.select(4), .width(32)) multiplexer_1 (
    .in0(fp_signed_inject_1_out_3), .in1(fp_signed_inject_negate_1_out_3),
    .in2(fp_signed_inject_xor_1_out_3), .in3({32{1'b0}}), .in4(fp_min_max_1_min), .in5(fp_min_max_1_max),
    .in6({32{1'b0}}), .in8(bit_extender_1_out), .in9(bit_extender_3_out), .in10(bit_extender_2_out),
    .in11({32{1'b0}}), .in12({32{1'b0}}), .in13({32{1'b0}}), .in14({32{1'b0}}), .in15({32{1'b0}}),
    .out(multiplexer_1_out), .sel(fp_mmnsc_reducer_1_out_2));  // open: in7
  fp_mmnsc_reducer fp_mmnsc_reducer_1 (.in_1(Funct73), .out_2(fp_mmnsc_reducer_1_out_2));
  fp_convert_reducer fp_convert_reducer_1 (.rs2(rs2), .func73(Funct73), .reduced(fp_convert_reducer_1_reduced));
  fp_convert_detector fp_convert_detector_1 (.func73(Funct73), .rs2(rs2), .out_3(fp_convert_detector_1_out_3));
  Multiplexer #(.select(4), .width(32)) multiplexer_2 (
    .in0({32{1'b0}}), .in1({32{1'b0}}), .in2({32{1'b0}}), .in3({32{1'b0}}), .in4(inttofp_1_p2),
    .in5(inttofp_2_p2), .in6({32{1'b0}}), .in7({32{1'b0}}), .in8({32{1'b0}}), .in9({32{1'b0}}),
    .in10(fptoint_1_p2), .in11(fptoint_1_p2), .in12({32{1'b0}}), .in13({32{1'b0}}), .in14({32{1'b0}}),
    .in15({32{1'b0}}), .out(multiplexer_2_out), .sel(fp_convert_reducer_1_reduced));
  Multiplexer #(.select(4), .width(32)) multiplexer_3 (
    .in0(fpadder_1_out), .in1({32{1'b0}}), .in2({32{1'b0}}), .in3(fpmultiplier_1_out), .in4({32{1'b0}}),
    .in5(fpsubtractor_1_out), .in6(fpdivider_1_out), .in7(fpsqr_wrapper_1_out_2), .in8({32{1'b0}}),
    .in9({32{1'b0}}), .in10({32{1'b0}}), .in11({32{1'b0}}), .in12({32{1'b0}}), .in13({32{1'b0}}),
    .in14({32{1'b0}}), .in15({32{1'b0}}), .out(multiplexer_3_out), .sel(Funct73[6:3]));
  fp_mmnsc_detector fp_mmnsc_detector_1 (.in_1(Funct73), .out_2(fp_mmnsc_detector_1_out_2));
  Multiplexer #(.select(2), .width(32)) multiplexer_4 (
    .in0(multiplexer_3_out), .in1(multiplexer_1_out), .in2(multiplexer_2_out), .in3({32{1'b0}}),
    .out(result), .sel(or_2_out));
  assign or_2_out = fp_convert_detector_1_out_3 | fp_mmnsc_detector_1_out_2;  // OR_Gate or_2, 2 bits wide

  // Notes on the sheet:
  //   Op2: initial=0x3
  //   Y Redondeo
endmodule

module ALU (
  input  [6:0] Func37,
  input  [31:0] Op1,
  input  [31:0] Op2,
  output [31:0] Result,
  output [2:0] CSR
);

  wire [31:0] adder_1_out, and_1_out, divider_1_out, divider_1_rem, divider_2_out, divider_2_rem,
       multiplier_1_cout, multiplier_2_cout, multiplier_2_out, or_1_out, shifter_1_out, shifter_2_out,
       shifter_3_out, subtractor_1_out, xor_1_out;

  assign and_1_out = Op1 & Op2;  // AND_Gate and_1, 32 bits wide
  assign or_1_out = Op1 | Op2;  // OR_Gate or_1, 32 bits wide
  assign xor_1_out = Op1 ^ Op2;  // XOR_Gate xor_1, 32 bits wide
  Adder #(.width(32)) adder_1 (.a(Op1), .b(Op2), .out(adder_1_out), .cout(CSR[2]));  // open: cin
  Subtractor #(.width(32)) subtractor_1 (.a(Op1), .b(Op2), .out(subtractor_1_out));  // open: bin, bout
  Shifter #(.width(32)) shifter_1 (.in(Op1), .\dist (Op2[4:0]), .out(shifter_1_out));
  Shifter #(.shift("lr"), .width(32)) shifter_2 (.in(Op1), .\dist (Op2[4:0]), .out(shifter_2_out));
  Shifter #(.shift("ar"), .width(32)) shifter_3 (.in(Op1), .\dist (Op2[4:0]), .out(shifter_3_out));
  Comparator #(.mode("unsigned"), .width(32)) comparator_1 (.a(Op1), .b(Op2), .lt(CSR[1]));  // open: gt, eq
  Comparator #(.width(32)) comparator_2 (.a(Op1), .b(Op2), .lt(CSR[1]));  // open: gt, eq
  Multiplier #(.width(32)) multiplier_1 (.a(Op1), .b(Op2), .cout(multiplier_1_cout));  // open: out, cin
  Multiplier #(.mode("twosComplement"), .width(32)) multiplier_2 (
    .a(Op1), .b(Op2), .out(multiplier_2_out), .cout(multiplier_2_cout));  // open: cin
  Divider #(.width(32)) divider_1 (.a(Op1), .b(Op2), .out(divider_1_out), .rem(divider_1_rem));  // open: upper
  Divider #(.mode("twosComplement"), .width(32)) divider_2 (
    .a(Op1), .b(Op2), .out(divider_2_out), .rem(divider_2_rem));  // open: upper
  Multiplexer #(.select(5), .width(32)) multiplexer_1 (
    .in0(adder_1_out), .in1(shifter_1_out), .in2({{31{1'b0}}, CSR[1]}), .in3({{31{1'b0}}, CSR[1]}),
    .in4(xor_1_out), .in5(shifter_2_out), .in6(or_1_out), .in7(and_1_out), .in8(subtractor_1_out),
    .in9({32{1'b0}}), .in10({32{1'b0}}), .in11({32{1'b0}}), .in12({32{1'b0}}), .in13(shifter_3_out),
    .in14({32{1'b0}}), .in15({32{1'b0}}), .in16(multiplier_2_out), .in17(multiplier_2_cout),
    .in18(multiplier_2_cout), .in19(multiplier_1_cout), .in20(divider_2_out), .in21(divider_1_out),
    .in22(divider_2_rem), .in23(divider_1_rem), .in24({32{1'b0}}), .in25({32{1'b0}}), .in26({32{1'b0}}),
    .in27({32{1'b0}}), .in28({32{1'b0}}), .in29({32{1'b0}}), .in30({32{1'b0}}), .in31({32{1'b0}}),
    .out(Result), .sel(Func37[4:0]));

  assign CSR[0] = CSR[1];

  // Notes on the sheet:
  //   sll
  //   srl
  //   sra
  //   sltu
  //   slt
  //   m
  //   mulu
  //   mul
  //   divu
  //   ru
  //   div
  //   rem
  //   first bit is X less than Y unsigned
  //   second bit is X less than Y signed
  //   third bit is overflow in sum
endmodule

module FPALU_3sr (
  input  [31:0] Op1,
  input  [31:0] Op2,
  input  [31:0] Op3,
  input  [2:0] Redondeo,
  output [31:0] Result
);
endmodule

module MU (
  input  [31:0] IMM,
  input  [31:0] RS1,
  input  [6:0] Funct73,
  output [31:0] Result
);

  wire [31:0] bit_extender_1_out, bit_extender_2_out, bit_extender_3_out, bit_extender_4_out,
       multiplexer_1_out;

  assign bit_extender_1_out = {{24{1'b1}}, IMM[7:0]};  // Bit_Extender bit_extender_1
  assign bit_extender_2_out = {{24{1'b0}}, IMM[7:0]};  // Bit_Extender bit_extender_2
  assign bit_extender_3_out = {{16{1'b1}}, IMM[15:0]};  // Bit_Extender bit_extender_3
  assign bit_extender_4_out = {{16{1'b0}}, IMM[15:0]};  // Bit_Extender bit_extender_4
  Multiplexer #(.select(3), .width(32)) multiplexer_1 (
    .in0(bit_extender_1_out), .in1(bit_extender_3_out), .in2(IMM), .in3(bit_extender_2_out),
    .in4(bit_extender_4_out), .in5({32{1'b0}}), .in6({32{1'b0}}), .in7({32{1'b0}}), .out(multiplexer_1_out),
    .sel(Funct73[2:0]));
  Adder #(.width(32)) adder_1 (.a(multiplexer_1_out), .b(RS1), .out(Result));  // open: cin, cout

  // Notes on the sheet:
  //   Byte
  //   ByteU
  //   Half
  //   HalfU
  //   Word
endmodule

module CU (
  input  [6:0] Opcode,
  input  [31:0] IMM,
  input  [23:0] PC,
  input  [31:0] RS1,
  input  [31:0] RS2,
  input  [6:0] Funct73,
  output Jump,
  output [31:0] Result
);

  wire comparator_1_eq, comparator_1_gt, comparator_1_lt, comparator_2_eq, comparator_2_gt, comparator_2_lt,
       multiplexer_1_out, not_1_out, or_1_out, or_2_out;
  wire [2:0] cuplexer_1_instruction;
  wire [31:0] adder_1_out, adder_2_out, bit_extender_1_out, controlled_buffer_1_out;

  assign bit_extender_1_out = {{8{1'b0}}, PC};  // Bit_Extender bit_extender_1
  Adder #(.width(32)) adder_1 (.a(IMM), .b(bit_extender_1_out), .out(adder_1_out));  // open: cin, cout
  Adder #(.width(32)) adder_2 (.a(IMM), .b(RS1), .out(adder_2_out));  // open: cin, cout
  Comparator #(.width(32)) comparator_1 (
    .a(RS1), .b(RS2), .gt(comparator_1_gt), .eq(comparator_1_eq), .lt(comparator_1_lt));
  Comparator #(.mode("unsigned"), .width(32)) comparator_2 (
    .a(RS1), .b(RS2), .gt(comparator_2_gt), .eq(comparator_2_eq), .lt(comparator_2_lt));
  not not_1 (not_1_out, comparator_1_eq);
  or or_1 (or_1_out, comparator_1_gt, comparator_1_eq);
  or or_2 (or_2_out, comparator_2_gt, comparator_2_eq);
  assign controlled_buffer_1_out = multiplexer_1_out ? adder_1_out : 32'bz;  // Controlled_Buffer controlled_buffer_1
  Multiplexer #(.select(3)) multiplexer_1 (
    .in0(comparator_1_eq), .in1(not_1_out), .in4(comparator_1_lt), .in5(or_1_out), .in6(comparator_2_lt),
    .in7(or_2_out), .out(multiplexer_1_out), .sel(Funct73[2:0]));  // open: in2, in3
  CUPlexer cuplexer_1 (.Opcode(Opcode), .Jump(Jump), .Instruction(cuplexer_1_instruction));
  Multiplexer #(.select(3), .width(32)) multiplexer_2 (
    .in0(IMM), .in1(adder_1_out), .in2(adder_2_out), .in3(controlled_buffer_1_out), .out(Result),
    .sel(cuplexer_1_instruction));  // open: in4, in5, in6, in7
endmodule

module VALU (
  input  [6:0] Func37,
  input  [31:0] Op1_1,
  input  [31:0] Op1_2,
  input  [31:0] Op1_3,
  input  [31:0] Op2_1,
  input  [31:0] Op2_2,
  input  [31:0] Op2_3,
  output [31:0] Out1,
  output [31:0] Out2,
  output [31:0] Out3
);

  wire [31:0] adder_1_out, adder_2_out, adder_3_out, multiplier_1_out, multiplier_2_out, multiplier_3_out;

  Adder #(.width(32)) adder_1 (.a(Op1_1), .b(Op2_1), .out(adder_1_out));  // open: cin, cout
  Adder #(.width(32)) adder_2 (.a(Op1_2), .b(Op2_2), .out(adder_2_out));  // open: cin, cout
  Adder #(.width(32)) adder_3 (.a(Op1_3), .b(Op2_3), .out(adder_3_out));  // open: cin, cout
  Multiplier #(.mode("twosComplement"), .width(32)) multiplier_1 (
    .a(Op1_1), .b(Op2_1), .out(multiplier_1_out));  // open: cin, cout
  Multiplier #(.mode("twosComplement"), .width(32)) multiplier_2 (
    .a(Op1_2), .b(Op2_2), .out(multiplier_2_out));  // open: cin, cout
  Multiplier #(.mode("twosComplement"), .width(32)) multiplier_3 (
    .a(Op1_3), .b(Op2_3), .out(multiplier_3_out));  // open: cin, cout
  Multiplexer #(.select(2), .width(32)) multiplexer_1 (
    .in0(adder_1_out), .in1({32{1'b0}}), .in2(multiplier_1_out), .in3({32{1'b0}}), .out(Out1),
    .sel(Func37[4:3]));
  Multiplexer #(.select(2), .width(32)) multiplexer_2 (
    .in0(adder_2_out), .in1({32{1'b0}}), .in2(multiplier_2_out), .in3({32{1'b0}}), .out(Out2),
    .sel(Func37[4:3]));
  Multiplexer #(.select(2), .width(32)) multiplexer_3 (
    .in0(adder_3_out), .in1({32{1'b0}}), .in2(multiplier_3_out), .in3({32{1'b0}}), .out(Out3),
    .sel(Func37[4:3]));
endmodule

module small_register_file (
  input  Clock,
  input  EnableX0,
  input  EnableWrite,
  input  [3:0] ReadRegisterY,
  input  EnableRead,
  input  [3:0] ReadRegisterX,
  input  [3:0] SetRegister,
  input  [31:0] Data,
  output [31:0] OutputY,
  output [31:0] OutputX
);

  wire and_1_out, decoder_1_out0, decoder_1_out1, decoder_1_out2, decoder_1_out3, decoder_1_out4,
       decoder_1_out5, decoder_1_out6, decoder_1_out7, decoder_1_out8, decoder_1_out9, decoder_1_out10,
       decoder_1_out11, decoder_1_out12, decoder_1_out13, decoder_1_out14, decoder_1_out15, ER0_out, ER1_out,
       ER2_out, ER3_out, ER4_out, ER5_out, ER6_out, ER7_out, ER8_out, ER9_out, ER10_out, ER11_out, ER12_out,
       ER13_out, ER14_out, ER15_out;
  wire [31:0] demultiplexer_1_out0, demultiplexer_1_out1, demultiplexer_1_out2, demultiplexer_1_out3,
       demultiplexer_1_out4, demultiplexer_1_out5, demultiplexer_1_out6, demultiplexer_1_out7,
       demultiplexer_1_out8, demultiplexer_1_out9, demultiplexer_1_out10, demultiplexer_1_out11,
       demultiplexer_1_out12, demultiplexer_1_out13, demultiplexer_1_out14, demultiplexer_1_out15,
       register_1_q, register_2_q, register_3_q, register_4_q, register_5_q, register_6_q, register_7_q,
       register_8_q, register_9_q, register_10_q, register_11_q, register_12_q, register_13_q, register_14_q,
       register_15_q, register_16_q;

  Decoder #(.enable("false"), .select(4)) decoder_1 (
    .out0(decoder_1_out0), .out1(decoder_1_out1), .out2(decoder_1_out2), .out3(decoder_1_out3),
    .out4(decoder_1_out4), .out5(decoder_1_out5), .out6(decoder_1_out6), .out7(decoder_1_out7),
    .out8(decoder_1_out8), .out9(decoder_1_out9), .out10(decoder_1_out10), .out11(decoder_1_out11),
    .out12(decoder_1_out12), .out13(decoder_1_out13), .out14(decoder_1_out14), .out15(decoder_1_out15),
    .sel(SetRegister));
  and ER0 (ER0_out, EnableWrite, decoder_1_out0);
  and ER1 (ER1_out, EnableWrite, decoder_1_out1);
  and ER2 (ER2_out, EnableWrite, decoder_1_out2);
  and ER3 (ER3_out, EnableWrite, decoder_1_out3);
  and ER4 (ER4_out, EnableWrite, decoder_1_out4);
  and ER5 (ER5_out, EnableWrite, decoder_1_out5);
  and ER6 (ER6_out, EnableWrite, decoder_1_out6);
  and ER7 (ER7_out, EnableWrite, decoder_1_out7);
  and ER8 (ER8_out, EnableWrite, decoder_1_out8);
  and ER9 (ER9_out, EnableWrite, decoder_1_out9);
  and ER10 (ER10_out, EnableWrite, decoder_1_out10);
  and ER11 (ER11_out, EnableWrite, decoder_1_out11);
  and ER12 (ER12_out, EnableWrite, decoder_1_out12);
  and ER13 (ER13_out, EnableWrite, decoder_1_out13);
  and ER14 (ER14_out, EnableWrite, decoder_1_out14);
  and ER15 (ER15_out, EnableWrite, decoder_1_out15);
  and and_1 (and_1_out, EnableX0, ER0_out);
  Register #(.width(32)) register_1 (
    .D(demultiplexer_1_out0), .en(and_1_out), .Q(register_1_q), .clk(Clock), .clr(1'b0));
  Register #(.width(32)) register_2 (.D(demultiplexer_1_out1), .en(ER1_out), .Q(register_2_q), .clk(Clock), .clr(1'b0));
  Register #(.width(32)) register_3 (.D(demultiplexer_1_out2), .en(ER2_out), .Q(register_3_q), .clk(Clock), .clr(1'b0));
  Register #(.width(32)) register_4 (.D(demultiplexer_1_out3), .en(ER3_out), .Q(register_4_q), .clk(Clock), .clr(1'b0));
  Register #(.width(32)) register_5 (.D(demultiplexer_1_out4), .en(ER4_out), .Q(register_5_q), .clk(Clock), .clr(1'b0));
  Register #(.width(32)) register_6 (.D(demultiplexer_1_out5), .en(ER5_out), .Q(register_6_q), .clk(Clock), .clr(1'b0));
  Register #(.width(32)) register_7 (.D(demultiplexer_1_out6), .en(ER6_out), .Q(register_7_q), .clk(Clock), .clr(1'b0));
  Register #(.width(32)) register_8 (.D(demultiplexer_1_out7), .en(ER7_out), .Q(register_8_q), .clk(Clock), .clr(1'b0));
  Demultiplexer #(.select(4), .width(32)) demultiplexer_1 (
    .out0(demultiplexer_1_out0), .out1(demultiplexer_1_out1), .out2(demultiplexer_1_out2),
    .out3(demultiplexer_1_out3), .out4(demultiplexer_1_out4), .out5(demultiplexer_1_out5),
    .out6(demultiplexer_1_out6), .out7(demultiplexer_1_out7), .out8(demultiplexer_1_out8),
    .out9(demultiplexer_1_out9), .out10(demultiplexer_1_out10), .out11(demultiplexer_1_out11),
    .out12(demultiplexer_1_out12), .out13(demultiplexer_1_out13), .out14(demultiplexer_1_out14),
    .out15(demultiplexer_1_out15), .in(Data), .sel(SetRegister));
  Register #(.width(32)) register_9 (.D(demultiplexer_1_out8), .en(ER8_out), .Q(register_9_q), .clk(Clock), .clr(1'b0));
  Register #(.width(32)) register_10 (
    .D(demultiplexer_1_out9), .en(ER9_out), .Q(register_10_q), .clk(Clock), .clr(1'b0));
  Register #(.width(32)) register_11 (
    .D(demultiplexer_1_out10), .en(ER10_out), .Q(register_11_q), .clk(Clock), .clr(1'b0));
  Register #(.width(32)) register_12 (
    .D(demultiplexer_1_out11), .en(ER11_out), .Q(register_12_q), .clk(Clock), .clr(1'b0));
  Register #(.width(32)) register_13 (
    .D(demultiplexer_1_out12), .en(ER12_out), .Q(register_13_q), .clk(Clock), .clr(1'b0));
  Register #(.width(32)) register_14 (
    .D(demultiplexer_1_out13), .en(ER13_out), .Q(register_14_q), .clk(Clock), .clr(1'b0));
  Register #(.width(32)) register_15 (
    .D(demultiplexer_1_out14), .en(ER14_out), .Q(register_15_q), .clk(Clock), .clr(1'b0));
  Register #(.width(32)) register_16 (
    .D(demultiplexer_1_out15), .en(ER15_out), .Q(register_16_q), .clk(Clock), .clr(1'b0));
  Multiplexer #(.enable("true"), .select(4), .width(32)) multiplexer_1 (
    .in0(register_1_q), .in1(register_2_q), .in2(register_3_q), .in3(register_4_q), .in4(register_5_q),
    .in5(register_6_q), .in6(register_7_q), .in7(register_8_q), .in8(register_9_q), .in9(register_10_q),
    .in10(register_11_q), .in11(register_12_q), .in12(register_13_q), .in13(register_14_q),
    .in14(register_15_q), .in15(register_16_q), .out(OutputY), .sel(ReadRegisterY), .en(EnableRead));
  Multiplexer #(.enable("true"), .select(4), .width(32)) multiplexer_2 (
    .in0(register_1_q), .in1(register_2_q), .in2(register_3_q), .in3(register_4_q), .in4(register_5_q),
    .in5(register_6_q), .in6(register_7_q), .in7(register_8_q), .in8(register_9_q), .in9(register_10_q),
    .in10(register_11_q), .in11(register_12_q), .in12(register_13_q), .in13(register_14_q),
    .in14(register_15_q), .in15(register_16_q), .out(OutputX), .sel(ReadRegisterX), .en(EnableRead));
endmodule

module small_vector_register_file (
  input  [31:0] inputA0,
  input  [31:0] inputA1,
  input  [31:0] inputA2,
  input  Clock,
  input  EnableWrite1,
  input  [3:0] WriteToResgisterX,
  input  [3:0] ClearRegisterX,
  input  [3:0] ClearRegisterY,
  input  ClearEnableX,
  input  ClearEnableY,
  input  [3:0] RegisterToReadX,
  input  [3:0] RegisterToReadY,
  output [31:0] X0,
  output [31:0] X1,
  output [31:0] X2,
  output [31:0] Y0,
  output [31:0] Y2,
  output [31:0] Y3
);

  wire ReadEnableController_output0, ReadEnableController_output1, ReadEnableController_output2,
       ReadEnableController_output3, ReadEnableController_output4, ReadEnableController_output5,
       ReadEnableController_output6, ReadEnableController_output7, ReadEnableController_output8,
       ReadEnableController_output9, ReadEnableController_output10, ReadEnableController_output11,
       ReadEnableController_output12, ReadEnableController_output13, ReadEnableController_output14,
       ReadEnableController_output15, WriteEnableController_output0, WriteEnableController_output1,
       WriteEnableController_output2, WriteEnableController_output3, WriteEnableController_output4,
       WriteEnableController_output5, WriteEnableController_output6, WriteEnableController_output7,
       WriteEnableController_output8, WriteEnableController_output9, WriteEnableController_output10,
       WriteEnableController_output11, WriteEnableController_output12, WriteEnableController_output13,
       WriteEnableController_output14, WriteEnableController_output15;
  wire [31:0] V0_output_0, V0_output_1, V0_output_2, V1_output_0, V1_output_1, V1_output_2, V2_output_0,
       V2_output_1, V2_output_2, V3_output_0, V3_output_1, V3_output_2, V4_output_0, V4_output_1,
       V4_output_2, V5_output_0, V5_output_1, V5_output_2, V6_output_0, V6_output_1, V6_output_2,
       V7_output_0, V7_output_1, V7_output_2, V8_output_0, V8_output_1, V8_output_2, V9_output_0,
       V9_output_1, V9_output_2, V10_output_0, V10_output_1, V10_output_2, V11_output_0, V11_output_1,
       V11_output_2, V12_output_0, V12_output_1, V12_output_2, V13_output_0, V13_output_1, V13_output_2,
       V14_output_0, V14_output_1, V14_output_2, V15_output_0, V15_output_1, V15_output_2;

  double_demux WriteEnableController (
    .Select1(WriteToResgisterX), .Select2(WriteToResgisterX), .Input1(EnableWrite1), .Input2(EnableWrite1),
    .Output0(WriteEnableController_output0), .Output1(WriteEnableController_output1),
    .Output9(WriteEnableController_output9), .Output10(WriteEnableController_output10),
    .output11(WriteEnableController_output11), .Output12(WriteEnableController_output12),
    .Output13(WriteEnableController_output13), .Output2(WriteEnableController_output2),
    .Output3(WriteEnableController_output3), .Output4(WriteEnableController_output4),
    .Output5(WriteEnableController_output5), .Output6(WriteEnableController_output6),
    .Output7(WriteEnableController_output7), .OUtput8(WriteEnableController_output8),
    .Output14(WriteEnableController_output14), .Output15(WriteEnableController_output15));
  double_demux ReadEnableController (
    .Select1(ClearRegisterX), .Select2(ClearRegisterY), .Input1(ClearEnableX), .Input2(ClearEnableY),
    .Output0(ReadEnableController_output0), .Output1(ReadEnableController_output1),
    .Output9(ReadEnableController_output9), .Output10(ReadEnableController_output10),
    .output11(ReadEnableController_output11), .Output12(ReadEnableController_output12),
    .Output13(ReadEnableController_output13), .Output2(ReadEnableController_output2),
    .Output3(ReadEnableController_output3), .Output4(ReadEnableController_output4),
    .Output5(ReadEnableController_output5), .Output6(ReadEnableController_output6),
    .Output7(ReadEnableController_output7), .OUtput8(ReadEnableController_output8),
    .Output14(ReadEnableController_output14), .Output15(ReadEnableController_output15));
  vector_register V0 (
    .Clock(Clock), .WriteEnable(WriteEnableController_output0), .Clear(ReadEnableController_output0),
    .Input_0(inputA0), .Input_1(inputA1), .Input_2(inputA2), .Output_0(V0_output_0), .Output_1(V0_output_1),
    .Output_2(V0_output_2));
  vector_register V8 (
    .Clock(Clock), .WriteEnable(WriteEnableController_output8), .Clear(ReadEnableController_output8),
    .Input_0(inputA0), .Input_1(inputA1), .Input_2(inputA2), .Output_0(V8_output_0), .Output_1(V8_output_1),
    .Output_2(V8_output_2));
  vector_register V9 (
    .Clock(Clock), .WriteEnable(WriteEnableController_output9), .Clear(ReadEnableController_output9),
    .Input_0(inputA0), .Input_1(inputA1), .Input_2(inputA2), .Output_0(V9_output_0), .Output_1(V9_output_1),
    .Output_2(V9_output_2));
  vector_register V1 (
    .Clock(Clock), .WriteEnable(WriteEnableController_output1), .Clear(ReadEnableController_output1),
    .Input_0(inputA0), .Input_1(inputA1), .Input_2(inputA2), .Output_0(V1_output_0), .Output_1(V1_output_1),
    .Output_2(V1_output_2));
  vector_register V10 (
    .Clock(Clock), .WriteEnable(WriteEnableController_output10), .Clear(ReadEnableController_output10),
    .Input_0(inputA0), .Input_1(inputA1), .Input_2(inputA2), .Output_0(V10_output_0),
    .Output_1(V10_output_1), .Output_2(V10_output_2));
  vector_register V2 (
    .Clock(Clock), .WriteEnable(WriteEnableController_output2), .Clear(ReadEnableController_output2),
    .Input_0(inputA0), .Input_1(inputA1), .Input_2(inputA2), .Output_0(V2_output_0), .Output_1(V2_output_1),
    .Output_2(V2_output_2));
  vector_register V11 (
    .Clock(Clock), .WriteEnable(WriteEnableController_output11), .Clear(ReadEnableController_output11),
    .Input_0(inputA0), .Input_1(inputA1), .Input_2(inputA2), .Output_0(V11_output_0),
    .Output_1(V11_output_1), .Output_2(V11_output_2));
  vector_register V3 (
    .Clock(Clock), .WriteEnable(WriteEnableController_output3), .Clear(ReadEnableController_output3),
    .Input_0(inputA0), .Input_1(inputA1), .Input_2(inputA2), .Output_0(V3_output_0), .Output_1(V3_output_1),
    .Output_2(V3_output_2));
  vector_register V12 (
    .Clock(Clock), .WriteEnable(WriteEnableController_output12), .Clear(ReadEnableController_output12),
    .Input_0(inputA0), .Input_1(inputA1), .Input_2(inputA2), .Output_0(V12_output_0),
    .Output_1(V12_output_1), .Output_2(V12_output_2));
  vector_register V4 (
    .Clock(Clock), .WriteEnable(WriteEnableController_output4), .Clear(ReadEnableController_output4),
    .Input_0(inputA0), .Input_1(inputA1), .Input_2(inputA2), .Output_0(V4_output_0), .Output_1(V4_output_1),
    .Output_2(V4_output_2));
  vector_register V5 (
    .Clock(Clock), .WriteEnable(WriteEnableController_output5), .Clear(ReadEnableController_output5),
    .Input_0(inputA0), .Input_1(inputA1), .Input_2(inputA2), .Output_0(V5_output_0), .Output_1(V5_output_1),
    .Output_2(V5_output_2));
  vector_register V13 (
    .Clock(Clock), .WriteEnable(WriteEnableController_output13), .Clear(ReadEnableController_output13),
    .Input_0(inputA0), .Input_1(inputA1), .Input_2(inputA2), .Output_0(V13_output_0),
    .Output_1(V13_output_1), .Output_2(V13_output_2));
  vector_register V6 (
    .Clock(Clock), .WriteEnable(WriteEnableController_output6), .Clear(ReadEnableController_output6),
    .Input_0(inputA0), .Input_1(inputA1), .Input_2(inputA2), .Output_0(V6_output_0), .Output_1(V6_output_1),
    .Output_2(V6_output_2));
  vector_register V14 (
    .Clock(Clock), .WriteEnable(WriteEnableController_output14), .Clear(ReadEnableController_output14),
    .Input_0(inputA0), .Input_1(inputA1), .Input_2(inputA2), .Output_0(V14_output_0),
    .Output_1(V14_output_1), .Output_2(V14_output_2));
  vector_register V7 (
    .Clock(Clock), .WriteEnable(WriteEnableController_output7), .Clear(ReadEnableController_output7),
    .Input_0(inputA0), .Input_1(inputA1), .Input_2(inputA2), .Output_0(V7_output_0), .Output_1(V7_output_1),
    .Output_2(V7_output_2));
  vector_register V15 (
    .Clock(Clock), .WriteEnable(WriteEnableController_output15), .Clear(ReadEnableController_output15),
    .Input_0(inputA0), .Input_1(inputA1), .Input_2(inputA2), .Output_0(V15_output_0),
    .Output_1(V15_output_1), .Output_2(V15_output_2));
  vector_mux vector_mux_1 (
    .input61(V6_output_1), .input62(V6_output_2), .input00(V0_output_0), .input70(V7_output_0),
    .input71(V7_output_1), .input72(V7_output_2), .input80(V8_output_0), .input81(V8_output_1),
    .input82(V8_output_2), .input90(V9_output_0), .input91(V9_output_1), .input92(V9_output_2),
    .input01(V0_output_1), .input100(V10_output_0), .input101(V10_output_1), .input102(V10_output_2),
    .input110(V11_output_0), .input111(V11_output_1), .input112(V11_output_2), .input120(V12_output_0),
    .input121(V12_output_1), .input02(V0_output_2), .input122(V12_output_2), .input130(V13_output_0),
    .input131(V13_output_1), .input132(V13_output_2), .input140(V14_output_0), .input141(V14_output_1),
    .input142(V14_output_2), .input150(V15_output_0), .input151(V15_output_1), .input152(V15_output_2),
    .input10(V1_output_0), .input11(V1_output_1), .input12(V1_output_2), .input20(V2_output_0),
    .input21(V2_output_1), .input22(V2_output_2), .input30(V3_output_0), .input31(V3_output_1),
    .input32(V3_output_2), .input40(V4_output_0), .input41(V4_output_1), .input42(V4_output_2),
    .input50(V5_output_0), .input51(V5_output_1), .input52(V5_output_2), .input60(V6_output_0),
    .selectBits(RegisterToReadX), .Output0(X0), .Output1(X1), .Output2(X2));
  vector_mux vector_mux_2 (
    .input61(V6_output_1), .input62(V6_output_2), .input00(V0_output_0), .input70(V7_output_0),
    .input71(V7_output_1), .input72(V7_output_2), .input80(V8_output_0), .input81(V8_output_1),
    .input82(V8_output_2), .input90(V9_output_0), .input91(V9_output_1), .input92(V9_output_2),
    .input01(V0_output_1), .input100(V10_output_0), .input101(V10_output_1), .input102(V10_output_2),
    .input110(V11_output_0), .input111(V11_output_1), .input112(V11_output_2), .input120(V12_output_0),
    .input121(V12_output_1), .input02(V0_output_2), .input122(V12_output_2), .input130(V13_output_0),
    .input131(V13_output_1), .input132(V13_output_2), .input140(V14_output_0), .input141(V14_output_1),
    .input142(V14_output_2), .input150(V15_output_0), .input151(V15_output_1), .input152(V15_output_2),
    .input10(V1_output_0), .input11(V1_output_1), .input12(V1_output_2), .input20(V2_output_0),
    .input21(V2_output_1), .input22(V2_output_2), .input30(V3_output_0), .input31(V3_output_1),
    .input32(V3_output_2), .input40(V4_output_0), .input41(V4_output_1), .input42(V4_output_2),
    .input50(V5_output_0), .input51(V5_output_1), .input52(V5_output_2), .input60(V6_output_0),
    .selectBits(RegisterToReadY), .Output0(Y0), .Output1(Y2), .Output2(Y3));
endmodule

module vector_register (
  input  WriteEnable,
  input  [31:0] Input_0,
  input  Clock,
  input  [31:0] Input_1,
  input  [31:0] Input_2,
  input  Clear,
  output [31:0] Output_0,
  output [31:0] Output_1,
  output [31:0] Output_2
);

  Register #(.width(32)) v_sub_0 (.D(Input_0), .en(WriteEnable), .clk(Clock), .Q(Output_0), .clr(Clear));
  Register #(.width(32)) v_sub_1 (.D(Input_1), .en(WriteEnable), .clk(Clock), .Q(Output_1), .clr(Clear));
  Register #(.width(32)) v_sub_2 (.D(Input_2), .en(WriteEnable), .clk(Clock), .Q(Output_2));  // open: clr
endmodule

module double_demux (
  input  [3:0] Select1,
  input  [3:0] Select2,
  input  Input2,
  input  Input1,
  output Output0,
  output Output1,
  output Output2,
  output Output3,
  output Output4,
  output Output5,
  output Output6,
  output Output7,
  output OUtput8,
  output Output9,
  output Output10,
  output output11,
  output Output12,
  output Output13,
  output Output14,
  output Output15
);

  wire demultiplexer_1_out0, demultiplexer_1_out1, demultiplexer_1_out2, demultiplexer_1_out3,
       demultiplexer_1_out4, demultiplexer_1_out5, demultiplexer_1_out6, demultiplexer_1_out7,
       demultiplexer_1_out8, demultiplexer_1_out9, demultiplexer_1_out10, demultiplexer_1_out11,
       demultiplexer_1_out12, demultiplexer_1_out13, demultiplexer_1_out14, demultiplexer_1_out15,
       demultiplexer_2_out0, demultiplexer_2_out1, demultiplexer_2_out2, demultiplexer_2_out3,
       demultiplexer_2_out4, demultiplexer_2_out5, demultiplexer_2_out6, demultiplexer_2_out7,
       demultiplexer_2_out8, demultiplexer_2_out9, demultiplexer_2_out10, demultiplexer_2_out11,
       demultiplexer_2_out12, demultiplexer_2_out13, demultiplexer_2_out14, demultiplexer_2_out15;

  Demultiplexer #(.select(4)) demultiplexer_1 (
    .out0(demultiplexer_1_out0), .out1(demultiplexer_1_out1), .out2(demultiplexer_1_out2),
    .out3(demultiplexer_1_out3), .out4(demultiplexer_1_out4), .out5(demultiplexer_1_out5),
    .out6(demultiplexer_1_out6), .out7(demultiplexer_1_out7), .out8(demultiplexer_1_out8),
    .out9(demultiplexer_1_out9), .out10(demultiplexer_1_out10), .out11(demultiplexer_1_out11),
    .out12(demultiplexer_1_out12), .out13(demultiplexer_1_out13), .out14(demultiplexer_1_out14),
    .out15(demultiplexer_1_out15), .in(Input1), .sel(Select1));
  Demultiplexer #(.select(4)) demultiplexer_2 (
    .out0(demultiplexer_2_out0), .out1(demultiplexer_2_out1), .out2(demultiplexer_2_out2),
    .out3(demultiplexer_2_out3), .out4(demultiplexer_2_out4), .out5(demultiplexer_2_out5),
    .out6(demultiplexer_2_out6), .out7(demultiplexer_2_out7), .out8(demultiplexer_2_out8),
    .out9(demultiplexer_2_out9), .out10(demultiplexer_2_out10), .out11(demultiplexer_2_out11),
    .out12(demultiplexer_2_out12), .out13(demultiplexer_2_out13), .out14(demultiplexer_2_out14),
    .out15(demultiplexer_2_out15), .in(Input2), .sel(Select2));
  or or_1 (Output0, demultiplexer_1_out0, demultiplexer_2_out0);
  or or_2 (Output1, demultiplexer_1_out1, demultiplexer_2_out1);
  or or_3 (Output2, demultiplexer_1_out2, demultiplexer_2_out2);
  or or_4 (Output3, demultiplexer_1_out3, demultiplexer_2_out3);
  or or_5 (Output4, demultiplexer_1_out4, demultiplexer_2_out4);
  or or_6 (Output5, demultiplexer_1_out5, demultiplexer_2_out5);
  or or_7 (Output6, demultiplexer_1_out6, demultiplexer_2_out6);
  or or_8 (Output7, demultiplexer_1_out7, demultiplexer_2_out7);
  or or_9 (OUtput8, demultiplexer_1_out8, demultiplexer_2_out8);
  or or_10 (Output9, demultiplexer_1_out9, demultiplexer_2_out9);
  or or_11 (Output10, demultiplexer_1_out10, demultiplexer_2_out10);
  or or_12 (output11, demultiplexer_1_out11, demultiplexer_2_out11);
  or or_13 (Output12, demultiplexer_1_out12, demultiplexer_2_out12);
  or or_14 (Output13, demultiplexer_1_out13, demultiplexer_2_out13);
  or or_15 (Output14, demultiplexer_1_out14, demultiplexer_2_out14);
  or or_16 (Output15, demultiplexer_1_out15, demultiplexer_2_out15);
endmodule

module vector_mux (
  input  [31:0] input00,
  input  [31:0] input01,
  input  [31:0] input02,
  input  [31:0] input10,
  input  [31:0] input11,
  input  [31:0] input12,
  input  [31:0] input20,
  input  [31:0] input21,
  input  [31:0] input22,
  input  [31:0] input30,
  input  [31:0] input31,
  input  [31:0] input32,
  input  [31:0] input40,
  input  [31:0] input41,
  input  [31:0] input42,
  input  [31:0] input50,
  input  [31:0] input51,
  input  [31:0] input52,
  input  [31:0] input60,
  input  [31:0] input61,
  input  [31:0] input62,
  input  [31:0] input70,
  input  [31:0] input71,
  input  [31:0] input72,
  input  [31:0] input80,
  input  [31:0] input81,
  input  [31:0] input82,
  input  [31:0] input90,
  input  [31:0] input91,
  input  [31:0] input92,
  input  [31:0] input100,
  input  [31:0] input101,
  input  [31:0] input102,
  input  [31:0] input110,
  input  [31:0] input111,
  input  [31:0] input112,
  input  [31:0] input120,
  input  [31:0] input121,
  input  [31:0] input122,
  input  [31:0] input130,
  input  [31:0] input131,
  input  [31:0] input132,
  input  [31:0] input140,
  input  [31:0] input141,
  input  [31:0] input142,
  input  [31:0] input150,
  input  [31:0] input151,
  input  [31:0] input152,
  input  [3:0] selectBits,
  output [31:0] Output0,
  output [31:0] Output1,
  output [31:0] Output2
);

  Multiplexer #(.select(4), .width(32)) multiplexer_1 (
    .in0(input00), .in1(input10), .in2(input20), .in3(input30), .in4(input40), .in5(input50), .in6(input60),
    .in7(input70), .in8(input80), .in9(input90), .in10(input100), .in11(input110), .in12(input120),
    .in13(input130), .in14(input140), .in15(input150), .out(Output0), .sel(selectBits));
  Multiplexer #(.select(4), .width(32)) multiplexer_2 (
    .in0(input01), .in1(input11), .in2(input21), .in3(input31), .in4(input41), .in5(input51), .in6(input61),
    .in7(input71), .in8(input81), .in9(input91), .in10(input101), .in11(input111), .in12(input121),
    .in13(input131), .in14(input141), .in15(input151), .out(Output1), .sel(selectBits));
  Multiplexer #(.select(4), .width(32)) multiplexer_3 (
    .in0(input02), .in1(input12), .in2(input22), .in3(input32), .in4(input42), .in5(input52), .in6(input62),
    .in7(input72), .in8(input82), .in9(input92), .in10(input102), .in11(input112), .in12(input122),
    .in13(input132), .in14(input142), .in15(input152), .out(Output2), .sel(selectBits));
endmodule

module decoder_unit (
  input  [31:0] Instruction,
  output [1:0] LoadR,
  output ALUImm,
  output StoreM,
  output [1:0] Unit,
  output [6:0] Opcode,
  output [4:0] RD,
  output [4:0] RS1,
  output [4:0] RS2,
  output [6:0] Funct37,
  output [31:0] Imm
);

  wire comparator_1_lt;
  wire [2:0] inst_type_idetifier_1_intype;
  wire [3:0] funct7_reducer_1_reduce;
  wire [10:0] bit_extender_4_out;
  wire [18:0] bit_extender_3_out;
  wire [19:0] bit_extender_1_out, bit_extender_2_out;

  assign bit_extender_1_out = {{19{Instruction[31]}}, Instruction[31]};  // Bit_Extender bit_extender_1
  assign bit_extender_2_out = {{19{Instruction[31]}}, Instruction[31]};  // Bit_Extender bit_extender_2
  assign bit_extender_3_out = {{18{Instruction[31]}}, Instruction[31]};  // Bit_Extender bit_extender_3
  assign bit_extender_4_out = {{10{Instruction[31]}}, Instruction[31]};  // Bit_Extender bit_extender_4
  funct7_Reducer funct7_reducer_1 (.Funct7(Instruction[31:25]), .Reduce(funct7_reducer_1_reduce));
  inst_type_idetifier inst_type_idetifier_1 (.Opcode(Instruction[6:0]), .InType(inst_type_idetifier_1_intype));
  Multiplexer #(.select(3), .width(32)) multiplexer_1 (
    .in1({bit_extender_1_out, Instruction[31:20]}),
    .in2({bit_extender_2_out, Instruction[31:25], Instruction[11:7]}),
    .in3({bit_extender_3_out, Instruction[31], Instruction[7], Instruction[30:25], Instruction[11:8], 1'b0}),
    .in4({Instruction[31:12], {12{1'b0}}}),
    .in5({bit_extender_4_out, Instruction[31], Instruction[19:12], Instruction[20], Instruction[30:21], 1'b0}),
    .in6({32{1'b0}}), .in7({32{1'b0}}), .out(Imm), .sel(inst_type_idetifier_1_intype));  // open: in0
  Multiplexer #(.width(4)) multiplexer_2 (
    .in0(funct7_reducer_1_reduce), .in1(4'b0000), .out(Funct37[6:3]), .sel(comparator_1_lt));
  Comparator #(.width(3)) comparator_1 (
    .a(3'b000), .b(inst_type_idetifier_1_intype), .lt(comparator_1_lt));  // open: gt, eq
  router router_1 (.Opcode(Instruction[6:0]), .ALUImm(ALUImm), .Unit(Unit), .ReadMem(StoreM), .WriteUnit(LoadR));

  assign Funct37[2:0] = Instruction[14:12];
  assign Opcode = Instruction[6:0];
  assign RD = Instruction[11:7];
  assign RS1 = Instruction[19:15];
  assign RS2 = Instruction[24:20];

  // Notes on the sheet:
  //   R-Type
  //   I-Type
  //   S-Type
  //   B-Type
  //   U-Type
  //   J-Type
  //   001
  //   010
  //   011
  //   100
  //   101
endmodule

module inst_type_idetifier (
  input  [6:0] Opcode,
  output [2:0] InType
);

  wire and_1_out, and_2_out, and_3_out, and_4_out, and_5_out, and_6_out, and_7_out, and_8_out, and_9_out,
       and_10_out, or_1_out, or_2_out;

  and and_1 (and_1_out, Opcode[0], Opcode[1], ~Opcode[2], ~Opcode[3], Opcode[4], Opcode[5], ~Opcode[6]);  // AND_Gate
  and and_2 (and_2_out, Opcode[0], Opcode[1], ~Opcode[2], ~Opcode[3], ~Opcode[4], ~Opcode[5], ~Opcode[6]);  // AND_Gate
  and and_3 (and_3_out, Opcode[0], Opcode[1], Opcode[2], ~Opcode[3], ~Opcode[4], Opcode[5], Opcode[6]);  // AND_Gate
  and and_4 (and_4_out, Opcode[0], Opcode[1], ~Opcode[2], ~Opcode[3], Opcode[4], ~Opcode[5], ~Opcode[6]);  // AND_Gate
  and and_5 (and_5_out, Opcode[0], Opcode[1], ~Opcode[2], ~Opcode[3], Opcode[4], Opcode[5], Opcode[6]);  // AND_Gate
  and and_6 (and_6_out, Opcode[0], Opcode[1], ~Opcode[2], ~Opcode[3], ~Opcode[4], Opcode[5], ~Opcode[6]);  // AND_Gate
  and and_7 (and_7_out, Opcode[0], Opcode[1], ~Opcode[2], ~Opcode[3], ~Opcode[4], Opcode[5], Opcode[6]);  // AND_Gate
  and and_8 (and_8_out, Opcode[0], Opcode[1], Opcode[2], ~Opcode[3], Opcode[4], Opcode[5], ~Opcode[6]);  // AND_Gate
  and and_9 (and_9_out, Opcode[0], Opcode[1], Opcode[2], ~Opcode[3], Opcode[4], ~Opcode[5], ~Opcode[6]);  // AND_Gate
  and and_10 (and_10_out, Opcode[0], Opcode[1], Opcode[2], Opcode[3], ~Opcode[4], Opcode[5], Opcode[6]);  // AND_Gate
  or or_1 (or_1_out, and_2_out, and_3_out, and_4_out, and_5_out);
  or or_2 (or_2_out, and_8_out, and_9_out);
  Priority_Encoder priority_encoder_1 (
    .in0(and_1_out), .in1(or_1_out), .in2(and_6_out), .in3(and_7_out), .in4(or_2_out), .in5(and_10_out),
    .in6(1'b0), .in7(1'b0), .out(InType));  // open: en_in, gs, en_out

  // Notes on the sheet:
  //   RType
  //   IType
  //   SType
  //   BType
  //   UType
  //   JType
endmodule

module funct7_Reducer (
  input  [6:0] Funct7,
  output [3:0] Reduce
);

  wire and_1_out, and_2_out, and_3_out, and_4_out, and_5_out, and_6_out, and_7_out, and_8_out, and_9_out,
       and_10_out, and_11_out, and_12_out, and_13_out, and_14_out, and_15_out;

  and and_1 (and_1_out, ~Funct7[0], ~Funct7[1], ~Funct7[2], ~Funct7[3], ~Funct7[4], ~Funct7[5], ~Funct7[6]);  // AND_Gate
  and and_2 (and_2_out, ~Funct7[0], ~Funct7[1], ~Funct7[2], ~Funct7[3], ~Funct7[4], Funct7[5], ~Funct7[6]);  // AND_Gate
  and and_3 (and_3_out, Funct7[0], ~Funct7[1], ~Funct7[2], ~Funct7[3], ~Funct7[4], ~Funct7[5], ~Funct7[6]);  // AND_Gate
  and and_4 (and_4_out, ~Funct7[0], ~Funct7[1], ~Funct7[2], Funct7[3], ~Funct7[4], ~Funct7[5], ~Funct7[6]);  // AND_Gate
  and and_5 (and_5_out, ~Funct7[0], ~Funct7[1], ~Funct7[2], Funct7[3], Funct7[4], ~Funct7[5], ~Funct7[6]);  // AND_Gate
  and and_6 (and_6_out, ~Funct7[0], ~Funct7[1], Funct7[2], ~Funct7[3], ~Funct7[4], ~Funct7[5], ~Funct7[6]);  // AND_Gate
  and and_7 (and_7_out, ~Funct7[0], ~Funct7[1], Funct7[2], Funct7[3], ~Funct7[4], ~Funct7[5], ~Funct7[6]);  // AND_Gate
  and and_8 (and_8_out, ~Funct7[0], ~Funct7[1], Funct7[2], Funct7[3], ~Funct7[4], Funct7[5], ~Funct7[6]);  // AND_Gate
  and and_9 (and_9_out, ~Funct7[0], ~Funct7[1], ~Funct7[2], ~Funct7[3], Funct7[4], ~Funct7[5], ~Funct7[6]);  // AND_Gate
  and and_10 (and_10_out, ~Funct7[0], ~Funct7[1], Funct7[2], ~Funct7[3], Funct7[4], ~Funct7[5], ~Funct7[6]);  // AND_Gate
  and and_11 (and_11_out, ~Funct7[0], ~Funct7[1], ~Funct7[2], ~Funct7[3], ~Funct7[4], Funct7[5], Funct7[6]);  // AND_Gate
  and and_12 (and_12_out, ~Funct7[0], ~Funct7[1], ~Funct7[2], ~Funct7[3], Funct7[4], Funct7[5], Funct7[6]);  // AND_Gate
  and and_13 (and_13_out, ~Funct7[0], ~Funct7[1], ~Funct7[2], ~Funct7[3], Funct7[4], ~Funct7[5], Funct7[6]);  // AND_Gate
  and and_14 (and_14_out, ~Funct7[0], ~Funct7[1], ~Funct7[2], Funct7[3], ~Funct7[4], Funct7[5], Funct7[6]);  // AND_Gate
  and and_15 (and_15_out, ~Funct7[0], ~Funct7[1], ~Funct7[2], Funct7[3], Funct7[4], Funct7[5], Funct7[6]);  // AND_Gate
  Priority_Encoder #(.select(4)) priority_encoder_1 (
    .in0(and_1_out), .in1(and_2_out), .in2(and_3_out), .in3(and_4_out), .in4(and_5_out), .in5(and_6_out),
    .in6(and_7_out), .in7(and_8_out), .in8(and_9_out), .in9(and_10_out), .in10(and_11_out),
    .in11(and_12_out), .in12(and_13_out), .in13(and_14_out), .in14(and_15_out), .out(Reduce));  // open: in15, gs, en_out, en_in

  // Notes on the sheet:
  //   SRAI - SUB -SRA
  //   MUL - MULH - MULHSU - MULHSU - MULHU - DIV - DIVU - REM - REMU
  //   SRET - WFI - FMUL
  //   MRET
  //   FSUB
  //   FDIV
  //   FSQRT
  //   FSGNJ - FSGNJN - FSGNJX
  //   FMIN - FMAX
  //   FCVT.W.S - FCVT.WU.S
  //   FMV - FCLASS
  //   FEQ - FLT - FLE
  //   FCVT.S.W - FCVT.S.WU
  //   FMV.W.X
  //   SLLI - SRLI - ADD - SLL - SLT - SLTU - XOR - SRL - OR - AND - FADD
endmodule

module router (
  input  [6:0] Opcode,
  output [1:0] WriteUnit,
  output ReadMem,
  output [1:0] Unit,
  output ALUImm
);

  wire ALUR_out, and_1_out, AUIPC_out, BRANCH_out, ECB_out, FALL_out, FENCE_out, FLW_out, FMADD_out,
       FMSUB_out, FNMADD_out, FNMSUB_out, FSW_out, JAL_out, JALR_out, LOAD_out, LUI_out, MINIV_out, or_1_out,
       or_2_out, or_3_out, or_4_out, or_5_out, or_6_out, or_7_out, STORE_out, VLD_out, VSD_out;

  and LUI (LUI_out, Opcode[0], Opcode[1], Opcode[2], ~Opcode[3], Opcode[4], Opcode[5], ~Opcode[6]);  // AND_Gate
  and AUIPC (AUIPC_out, Opcode[0], Opcode[1], Opcode[2], ~Opcode[3], Opcode[4], ~Opcode[5], ~Opcode[6]);  // AND_Gate
  and JAL (JAL_out, Opcode[0], Opcode[1], Opcode[2], Opcode[3], ~Opcode[4], Opcode[5], Opcode[6]);  // AND_Gate
  and JALR (JALR_out, Opcode[0], Opcode[1], Opcode[2], ~Opcode[3], ~Opcode[4], Opcode[5], Opcode[6]);  // AND_Gate
  and BRANCH (BRANCH_out, Opcode[0], Opcode[1], ~Opcode[2], ~Opcode[3], ~Opcode[4], Opcode[5], Opcode[6]);  // AND_Gate
  and FENCE (FENCE_out, Opcode[0], Opcode[1], Opcode[2], Opcode[3], ~Opcode[4], ~Opcode[5], ~Opcode[6]);  // AND_Gate
  and ECB (ECB_out, Opcode[0], Opcode[1], ~Opcode[2], ~Opcode[3], Opcode[4], Opcode[5], Opcode[6]);  // AND_Gate
  and STORE (STORE_out, Opcode[0], Opcode[1], ~Opcode[2], ~Opcode[3], ~Opcode[4], Opcode[5], ~Opcode[6]);  // AND_Gate
  and LOAD (LOAD_out, Opcode[0], Opcode[1], ~Opcode[2], ~Opcode[3], ~Opcode[4], ~Opcode[5], ~Opcode[6]);  // AND_Gate
  and FLW (FLW_out, Opcode[0], Opcode[1], Opcode[2], ~Opcode[3], ~Opcode[4], ~Opcode[5], ~Opcode[6]);  // AND_Gate
  and FSW (FSW_out, Opcode[0], Opcode[1], Opcode[2], ~Opcode[3], ~Opcode[4], Opcode[5], ~Opcode[6]);  // AND_Gate
  and VLD (VLD_out, Opcode[0], Opcode[1], Opcode[2], ~Opcode[3], Opcode[4], ~Opcode[5], Opcode[6]);  // AND_Gate
  and VSD (VSD_out, Opcode[0], Opcode[1], ~Opcode[2], Opcode[3], Opcode[4], ~Opcode[5], Opcode[6]);  // AND_Gate
  and ALUI (ALUImm, Opcode[0], Opcode[1], ~Opcode[2], ~Opcode[3], Opcode[4], ~Opcode[5], ~Opcode[6]);  // AND_Gate
  and ALUR (ALUR_out, Opcode[0], Opcode[1], ~Opcode[2], ~Opcode[3], Opcode[4], Opcode[5], ~Opcode[6]);  // AND_Gate
  and MINIV (MINIV_out, Opcode[0], Opcode[1], ~Opcode[2], ~Opcode[3], Opcode[4], ~Opcode[5], Opcode[6]);  // AND_Gate
  and FMADD (FMADD_out, Opcode[0], Opcode[1], ~Opcode[2], ~Opcode[3], ~Opcode[4], ~Opcode[5], Opcode[6]);  // AND_Gate
  and FMSUB (FMSUB_out, Opcode[0], Opcode[1], Opcode[2], ~Opcode[3], ~Opcode[4], ~Opcode[5], Opcode[6]);  // AND_Gate
  and FNMADD (FNMADD_out, Opcode[0], Opcode[1], Opcode[2], Opcode[3], ~Opcode[4], ~Opcode[5], Opcode[6]);  // AND_Gate
  and FNMSUB (FNMSUB_out, Opcode[0], Opcode[1], ~Opcode[2], Opcode[3], ~Opcode[4], ~Opcode[5], Opcode[6]);  // AND_Gate
  and FALL (FALL_out, Opcode[0], Opcode[1], ~Opcode[2], Opcode[3], ~Opcode[4], ~Opcode[5], Opcode[6]);  // AND_Gate
  or or_1 (or_1_out, ALUImm, ALUR_out);
  or or_2 (or_2_out, LUI_out, AUIPC_out, JAL_out, JALR_out, BRANCH_out, FENCE_out, ECB_out);
  or or_3 (or_3_out, STORE_out, LOAD_out, FLW_out, FSW_out, VLD_out, VSD_out);
  or or_4 (or_4_out, FMADD_out, FMSUB_out, FNMADD_out, FNMSUB_out, FALL_out);
  and and_1 (and_1_out, or_2_out, ~BRANCH_out, ~FENCE_out, ~ECB_out);  // AND_Gate
  Priority_Encoder #(.select(2)) priority_encoder_1 (
    .in0(or_1_out), .in1(or_3_out), .in2(or_2_out), .in3(1'b0), .out(Unit));  // open: gs, en_out, en_in
  or or_5 (or_5_out, and_1_out, LOAD_out, or_1_out);
  or or_6 (or_6_out, VLD_out, MINIV_out);
  or or_7 (or_7_out, FLW_out, or_4_out);
  or or_8 (ReadMem, STORE_out, FSW_out, VSD_out);
  Priority_Encoder #(.select(2)) priority_encoder_2 (
    .in1(or_5_out), .in2(or_6_out), .in3(or_7_out), .out(WriteUnit));  // open: in0, gs, en_out, en_in

  // Notes on the sheet:
  //   Arithmetic-Logic with Immediate
  //   Arithmetic-Logic with register
  //   CU
  //   MU
  //   ALU
  //   VALU
  //   FPALU
endmodule

module register_file (
  input  [31:0] Data,
  input  [4:0] RD,
  input  Write,
  input  [4:0] RX,
  input  [4:0] RY,
  input  Clock,
  output [31:0] OutputX,
  output [31:0] OutputY
);

  wire demultiplexer_1_out0, demultiplexer_1_out1;
  wire [31:0] small_register_file_1_outputx, small_register_file_1_outputy, small_register_file_2_outputx,
       small_register_file_2_outputy;

  Demultiplexer demultiplexer_1 (.out0(demultiplexer_1_out0), .out1(demultiplexer_1_out1), .in(Write), .sel(RD[4]));
  small_register_file small_register_file_1 (
    .Clock(Clock), .EnableX0(1'b0), .EnableWrite(demultiplexer_1_out0), .SetRegister(RD[3:0]), .Data(Data),
    .ReadRegisterY(RY[3:0]), .ReadRegisterX(RX[3:0]), .EnableRead(1'b1),
    .OutputY(small_register_file_1_outputy), .OutputX(small_register_file_1_outputx));
  small_register_file small_register_file_2 (
    .Clock(Clock), .EnableX0(1'b1), .EnableWrite(demultiplexer_1_out1), .SetRegister(RD[3:0]), .Data(Data),
    .ReadRegisterY(RY[3:0]), .ReadRegisterX(RX[3:0]), .EnableRead(1'b1),
    .OutputY(small_register_file_2_outputy), .OutputX(small_register_file_2_outputx));
  Multiplexer #(.width(32)) multiplexer_1 (
    .in0(small_register_file_1_outputx), .in1(small_register_file_2_outputx), .out(OutputX), .sel(RX[4]));
  Multiplexer #(.width(32)) multiplexer_2 (
    .in0(small_register_file_1_outputy), .in1(small_register_file_2_outputy), .out(OutputY), .sel(RY[4]));
endmodule

module vector_register_file (
  input  [31:0] Data1,
  input  [31:0] Data2,
  input  [31:0] Data3,
  input  [4:0] RD,
  input  Write,
  input  [4:0] RX,
  input  [4:0] RY,
  input  Clock,
  output [31:0] OutputX1,
  output [31:0] OutputX2,
  output [31:0] OutputX3,
  output [31:0] OutputY1,
  output [31:0] OutputY2,
  output [31:0] OutputY3
);

  wire demultiplexer_1_out0, demultiplexer_1_out1;
  wire [31:0] small_vector_register_file_1_x0, small_vector_register_file_1_x1,
       small_vector_register_file_1_x2, small_vector_register_file_1_y0, small_vector_register_file_1_y2,
       small_vector_register_file_1_y3, small_vector_register_file_2_x0, small_vector_register_file_2_x1,
       small_vector_register_file_2_x2, small_vector_register_file_2_y0, small_vector_register_file_2_y2,
       small_vector_register_file_2_y3;

  Demultiplexer demultiplexer_1 (.out0(demultiplexer_1_out0), .out1(demultiplexer_1_out1), .in(Write), .sel(RD[4]));
  small_vector_register_file small_vector_register_file_1 (
    .inputA2(Data3), .inputA0(Data1), .inputA1(Data2), .RegisterToReadX(RX[3:0]), .RegisterToReadY(RY[3:0]),
    .EnableWrite1(demultiplexer_1_out0), .ClearEnableX(1'b0), .ClearEnableY(1'b0), .Clock(Clock),
    .ClearRegisterX(4'b0000), .ClearRegisterY(4'b0000), .WriteToResgisterX(RD[3:0]),
    .X2(small_vector_register_file_1_x2), .Y0(small_vector_register_file_1_y0),
    .Y2(small_vector_register_file_1_y2), .Y3(small_vector_register_file_1_y3),
    .X0(small_vector_register_file_1_x0), .X1(small_vector_register_file_1_x1));
  small_vector_register_file small_vector_register_file_2 (
    .inputA2(Data3), .inputA0(Data1), .inputA1(Data2), .RegisterToReadX(RX[3:0]), .RegisterToReadY(RY[3:0]),
    .EnableWrite1(demultiplexer_1_out1), .ClearEnableX(1'b0), .ClearEnableY(1'b0), .Clock(Clock),
    .ClearRegisterX(4'b0000), .ClearRegisterY(4'b0000), .WriteToResgisterX(RD[3:0]),
    .X2(small_vector_register_file_2_x2), .Y0(small_vector_register_file_2_y0),
    .Y2(small_vector_register_file_2_y2), .Y3(small_vector_register_file_2_y3),
    .X0(small_vector_register_file_2_x0), .X1(small_vector_register_file_2_x1));
  Multiplexer #(.width(32)) multiplexer_1 (
    .in0(small_vector_register_file_1_x0), .in1(small_vector_register_file_2_x0), .out(OutputX1), .sel(RX[4]));
  Multiplexer #(.width(32)) multiplexer_2 (
    .in0(small_vector_register_file_1_x1), .in1(small_vector_register_file_2_x1), .out(OutputX2), .sel(RX[4]));
  Multiplexer #(.width(32)) multiplexer_3 (
    .in0(small_vector_register_file_1_x2), .in1(small_vector_register_file_2_x2), .out(OutputX3), .sel(RX[4]));
  Multiplexer #(.width(32)) multiplexer_4 (
    .in0(small_vector_register_file_1_y0), .in1(small_vector_register_file_2_y0), .out(OutputY1), .sel(RY[4]));
  Multiplexer #(.width(32)) multiplexer_5 (
    .in0(small_vector_register_file_1_y2), .in1(small_vector_register_file_2_y2), .out(OutputY2), .sel(RY[4]));
  Multiplexer #(.width(32)) multiplexer_6 (
    .in0(small_vector_register_file_1_y3), .in1(small_vector_register_file_2_y3), .out(OutputY3), .sel(RY[4]));
endmodule

module CUPlexer (
  input  [6:0] Opcode,
  output Jump,
  output [2:0] Instruction
);

  wire AUIPC_out, BRANCH_out, ECB_out, FENCE_out, JAL_out, JALR_out, LUI_out, or_1_out;

  and LUI (LUI_out, Opcode[0], Opcode[1], Opcode[2], ~Opcode[3], Opcode[4], Opcode[5], ~Opcode[6]);  // AND_Gate
  and AUIPC (AUIPC_out, Opcode[0], Opcode[1], Opcode[2], ~Opcode[3], Opcode[4], ~Opcode[5], ~Opcode[6]);  // AND_Gate
  and JAL (JAL_out, Opcode[0], Opcode[1], Opcode[2], Opcode[3], ~Opcode[4], Opcode[5], Opcode[6]);  // AND_Gate
  and JALR (JALR_out, Opcode[0], Opcode[1], Opcode[2], ~Opcode[3], ~Opcode[4], Opcode[5], Opcode[6]);  // AND_Gate
  and BRANCH (BRANCH_out, Opcode[0], Opcode[1], ~Opcode[2], ~Opcode[3], ~Opcode[4], Opcode[5], Opcode[6]);  // AND_Gate
  and FENCE (FENCE_out, Opcode[0], Opcode[1], Opcode[2], Opcode[3], ~Opcode[4], ~Opcode[5], ~Opcode[6]);  // AND_Gate
  and ECB (ECB_out, Opcode[0], Opcode[1], ~Opcode[2], ~Opcode[3], Opcode[4], Opcode[5], Opcode[6]);  // AND_Gate
  or or_1 (or_1_out, AUIPC_out, JAL_out);
  or or_2 (Jump, JAL_out, JALR_out, BRANCH_out);
  Priority_Encoder priority_encoder_1 (
    .in0(LUI_out), .in1(or_1_out), .in2(JALR_out), .in3(BRANCH_out), .in4(FENCE_out), .in5(ECB_out),
    .out(Instruction));  // open: in6, in7, en_in, gs, en_out
endmodule

module fpsqr_wrapper (
  input  [31:0] operand1,
  output [31:0] out_2
);


  assign out_2 = operand1;
endmodule

module fp_mmnsc_reducer (
  input  [6:0] in_1,
  output [3:0] out_2
);


  assign out_2 = {in_1[5], in_1[3], in_1[1:0]};
endmodule

module fp_mmnsc_detector (
  input  [6:0] in_1,
  output [1:0] out_2
);

  fp_mmnsc_bit_stream_detector fp_mmnsc_bit_stream_detector_1 (.input_bits(in_1), .match_found(out_2[0]));

  assign out_2[1] = 1'b0;

  // Notes on the sheet:
  //   identifica microinstrucciones para FMIN ||FSGNJ || FSGNJN -|| FSGNJX - || FMINAX || FEQ || FLT || FLE
endmodule

module fp_convert_reducer (
  input  [6:0] func73,
  input  [4:0] rs2,
  output [3:0] reduced
);


  assign reduced = {func73[5:3], rs2[0]};

  // Notes on the sheet:
  //   reductor de micro instrucciones convert
endmodule

module fp_convert_detector (
  input  [4:0] rs2,
  input  [6:0] func73,
  output [1:0] out_3
);

  fp_convert_bit_stream_detector fp_convert_bit_stream_detector_1 (.input_bits({func73[6:3], rs2}), .output_two(out_3));

  // Notes on the sheet:
  //   Detector de micro instrucciones convert
endmodule

module fp_min_max (
  input  [31:0] operand1,
  input  [31:0] operand2,
  output [31:0] max,
  output [31:0] min
);

  wire fpcomparator_1_p3;

  // FPComparator fpcomparator_1: pin names not known; wires that end beside it: operand1, operand2, fpcomparator_1_p3
  Multiplexer #(.width(32)) multiplexer_1 (.in0(operand2), .in1(operand1), .out(max), .sel(fpcomparator_1_p3));
  Multiplexer #(.width(32)) multiplexer_2 (.in0(operand1), .in1(operand2), .out(min), .sel(fpcomparator_1_p3));

  // Notes on the sheet:
  //   floating point min max
endmodule

module UnitSelector (
  input  [2:0] Unit,
  input  Write,
  output out_3,
  output out_4,
  output out_5,
  output out_6,
  output out_7,
  output out_8
);
endmodule

module fp_signed_inject (
  input  [31:0] in_1,
  input  [31:0] in_2,
  output [31:0] out_3
);


  assign out_3 = {in_2[31], in_1[30:0]};

  // Notes on the sheet:
  //   sign inject
endmodule

module fp_signed_inject_negate (
  input  [31:0] in_1,
  input  [31:0] in_2,
  output [31:0] out_3
);

  not not_1 (out_3[31], in_2[31]);

  assign out_3[30:0] = in_1[30:0];

  // Notes on the sheet:
  //   sign inject negate
endmodule

module fp_signed_inject_xor (
  input  [31:0] in_1,
  input  [31:0] in_2,
  output [31:0] out_3
);

  xor xor_1 (out_3[31], in_1[31], in_2[31]);

  assign out_3[30:0] = in_1[30:0];
endmodule

module valu_vmacc (
  input  [31:0] in_1,
  input  [31:0] in_2,
  input  [31:0] in_3,
  input  [31:0] in_4,
  input  [31:0] in_5,
  input  [31:0] in_6
);

  wire [31:0] multiplier_1_out, multiplier_2_out, multiplier_3_out;

  Multiplier #(.mode("twosComplement"), .width(32)) multiplier_1 (
    .a(in_1), .b(in_4), .out(multiplier_1_out));  // open: cin, cout
  Multiplier #(.mode("twosComplement"), .width(32)) multiplier_2 (
    .a(in_2), .b(in_5), .out(multiplier_2_out));  // open: cin, cout
  Multiplier #(.mode("twosComplement"), .width(32)) multiplier_3 (
    .a(in_3), .b(in_6), .out(multiplier_3_out));  // open: cin, cout
endmodule

module forwarding_unit (
  input  [31:0] rs1_value,
  input  [31:0] rs2_value,
  input  [31:0] imm_value,
  input  [4:0] rs1,
  input  [4:0] rs2,
  input  [4:0] rd,
  input  is_immediate,
  input  [31:0] forwarded_value,
  output [31:0] op1,
  output [31:0] op2
);

  wire comparator_1_eq;
  wire [1:0] bit_extender_1_out, or_2_out;
  wire [1:1] comparator_2_eq;
  wire [4:0] or_1_out;
  wire [31:0] or_3_out;

  assign bit_extender_1_out = {{1{1'b0}}, is_immediate};  // Bit_Extender bit_extender_1
  assign or_1_out = rd | {5{1'b0}};  // OR_Gate or_1, 5 bits wide
  Comparator #(.mode("unsigned"), .width(5)) comparator_1 (
    .a(or_1_out), .b(rs1), .eq(comparator_1_eq));  // open: gt, lt
  Comparator #(.mode("unsigned"), .width(5)) comparator_2 (
    .a(or_1_out), .b(rs2), .eq(comparator_2_eq[1]));  // open: gt, lt
  assign or_2_out = {comparator_2_eq[1], 1'b0} | bit_extender_1_out;  // OR_Gate or_2, 2 bits wide
  Multiplexer #(.select(2), .width(32)) multiplexer_1 (
    .in0(rs2_value), .in1(imm_value), .in2(or_3_out), .in3(or_3_out), .out(op2), .sel(or_2_out));
  assign or_3_out = forwarded_value | {32{1'b0}};  // OR_Gate or_3, 32 bits wide
  Multiplexer #(.width(32)) multiplexer_2 (.in0(rs1_value), .in1(or_3_out), .out(op1), .sel(comparator_1_eq));
endmodule

// VHDL entity fp_mmnsc_bit_stream_detector, as the project stores it:
--------------------------------------------------------------------------------
-- Project : cpu_risc_v
-- File    : fp_mmnsc_bit_stream_detector
-- Autor   : A. Badilla Olivas
-- Date    : 05/2024
--
--------------------------------------------------------------------------------
-- Description :
-- Identifies this funct73, the funct73 is a reduced version of the bits of funct 7 and 3.
-- 1000 000 || FSGNJ
-- 1000 001 || FSGNJN
-- 1000 010 || FSGNJX
-- 1001 000 || FMIN
-- 1001 001 || FMAX
-- 1100 010 || FEQ
-- 1100 001 || FLT
-- 1100 000 || FLE
-- mmnc stands for: min max negate signed compare instructions
--------------------------------------------------------------------------------
library ieee;
use ieee.std_logic_1164.all;
-- Definition of the interface of the fpga
entity fp_mmnsc_bit_stream_detector is
    port (
        input_bits : in std_logic_vector(6 downto 0);
        match_found : out std_logic                
    );
end entity fp_mmnsc_bit_stream_detector;
-- Behavioral description of the fpga
architecture behavioral of fp_mmnsc_bit_stream_detector is
begin
    process(input_bits)
    begin
        case input_bits is
            when "1000000" | "1000001" | "1000010" | "1001000" | "1001001" |
                 "1100010" | "1100001" | "1100000" =>
                match_found <= '1';
            when others =>
                match_found <= '0';
        end case;
    end process;
end architecture behavioral;

// VHDL entity fp_convert_bit_stream_detector, as the project stores it:
--------------------------------------------------------------------------------
-- Project : cpu_risc_v
-- File    : fp_convert_bit_stream_detector
-- Autor   : A. Badilla Olivas
-- Date    : 05/2024
--
--------------------------------------------------------------------------------
-- Description :
-- Identifies this funct73, the funct73 is a reduced version of the bits of funct 7 and 3 and rs2 for convert instructions
-- 1010 00000 || FCVT.W.S 
-- 1010 00001 || FCVT.WU.S 
-- 1101 00000 || FCVT.S.W 
-- 1101 00001 || FCVT.S.WU 
-- outputs 10 in if detected
--------------------------------------------------------------------------------

library ieee;
use ieee.std_logic_1164.all;

entity fp_convert_bit_stream_detector is
  port (
    input_bits  : in  std_logic_vector(8 downto 0); 
    output_two : out std_logic_vector(1 downto 0) 
  );
end entity fp_convert_bit_stream_detector;

architecture behavioral of fp_convert_bit_stream_detector is
begin
  process(input_bits)
  begin
    if (input_bits = "101000000" or input_bits = "101000001" or
        input_bits = "110100000" or input_bits = "110100001") then
      output_two <= "10"; 
    else
      output_two <= "00";
    end if;
  end process;
end architecture behavioral;

// VHDL entity cache_memory, as the project stores it:
library ieee;
use ieee.std_logic_1164.all;
use ieee.numeric_std.all;

entity cache_memory is
    port (
        clk         : in  std_logic;
        reset       : in  std_logic;
        cpu_address : in  std_logic_vector(31 downto 0); -- CPU address (assume 32-bit)
        cpu_read    : in  std_logic;                     -- CPU read request
        cpu_data_out: out std_logic_vector(63 downto 0); -- 64-bit data output to CPU

        ram_address : out std_logic_vector(31 downto 0); -- Address output to RAM
        ram_data_in : in  std_logic_vector(31 downto 0); -- 32-bit data input from RAM
        ram_read    : out std_logic                      -- Read enable signal to RAM
    );
end entity cache_memory;

architecture rtl of cache_memory is
    -- Constants
    constant PAGE_SIZE    : integer := 1024; -- Size of a page in bits
    constant WORDS_PER_PAGE : integer := PAGE_SIZE / 32; -- Number of 32-bit words per page
    constant CACHE_LINES  : integer := 4;    -- Number of cache lines (pages)

    -- Types
    type cache_line_type is record
        valid : std_logic;
        tag   : std_logic_vector(26 downto 0); -- Tag bits (32 - 2 (address) - 3 (word offset))
        data  : std_logic_vector(PAGE_SIZE-1 downto 0);
    end record;
    type cache_array_type is array (0 to CACHE_LINES-1) of cache_line_type;

    -- Signals
    signal cache         : cache_array_type;
    signal cache_address : std_logic_vector(1 downto 0); -- Address within the cache (2 bits)
    signal word_offset   : std_logic_vector(2 downto 0); -- Word offset within a page (3 bits)
    signal cache_hit     : std_logic;
    signal output_word   : std_logic_vector(31 downto 0); -- Temporary 32-bit word output
    signal ram_read_int  : std_logic;                      -- Intermediate signal for ram_read

begin

    -- Address decoding
    cache_address <= cpu_address(3 downto 2); -- Extract cache address bits
    word_offset   <= cpu_address(4 downto 2); -- Extract word offset bits

    -- Cache hit logic
    cache_hit <= '1' when cache(to_integer(unsigned(cache_address))).valid = '1' and
                        cache(to_integer(unsigned(cache_address))).tag = cpu_address(31 downto 5)
                else '0';

    -- RAM control process
    process (clk, reset)
    begin
        if reset = '1' then
            ram_read_int <= '0';
        elsif rising_edge(clk) then
            if cpu_read = '1' and cache_hit = '0' then -- Cache miss, read from RAM
                ram_read_int <= '1';
                ram_address <= cpu_address(31 downto 5) & "00000"; -- Page address in RAM
            else
                ram_read_int <= '0';
            end if;
        end if;
    end process;

    -- Cache data loading process
    process (clk, reset)
    begin
        if reset = '1' then
            for i in cache'range loop
                cache(i).valid <= '0';
            end loop;
        elsif rising_edge(clk) then
            if ram_read_int = '1' then -- Loading data from RAM
                cache(to_integer(unsigned(cache_address))).data((to_integer(unsigned(word_offset))+1)*32-1 downto to_integer(unsigned(word_offset))*32) <= ram_data_in;
                if word_offset = "111" then -- Last word of the page loaded
                    cache(to_integer(unsigned(cache_address))).valid <= '1';
                    cache(to_integer(unsigned(cache_address))).tag   <= cpu_address(31 downto 5);
                end if;
            end if;
        end if;
    end process;

    -- Data output to CPU
    process (clk)
    begin
        if rising_edge(clk) then
            if cpu_read = '1' then
                if cache_hit = '1' then
                    output_word <= cache(to_integer(unsigned(cache_address))).data((to_integer(unsigned(word_offset))+1)*32-1 downto to_integer(unsigned(word_offset))*32);
                else
                    output_word <= (others => '0'); -- Default output on cache miss (can be improved)
                end if;
            end if;
        end if;
    end process;

    -- Assemble 64-bit output from two 32-bit words
    cpu_data_out <= cache(to_integer(unsigned(cache_address))).data((to_integer(unsigned(word_offset))+2)*32-1 downto (to_integer(unsigned(word_offset))+1)*32) & output_word;

    -- Assign intermediate signal to output port
    ram_read <= ram_read_int;

end architecture rtl;
